// Logisim project sixteen-bit-computer.circ as structural Verilog: 17 circuits, main circuit main
module main (
  input  in_1,
  input  in_2,
  output out_3,
  output out_4,
  output out_5,
  output [15:0] out_6,
  output out_7,
  output out_8,
  output [15:0] out_9,
  output out_10,
  output out_11,
  output out_12,
  output [15:0] out_13,
  output out_14,
  output out_15,
  output [15:0] out_16,
  output out_17,
  output out_18,
  output out_19,
  output out_20,
  output out_21,
  output [15:0] out_22,
  output out_23,
  output out_24,
  output out_25,
  output out_26,
  output out_27,
  output out_28,
  output out_29,
  output out_30,
  output out_31,
  output [15:0] out_32,
  output out_33,
  output out_34,
  output out_35,
  output out_36,
  output out_37,
  output out_38,
  output out_39,
  output out_40,
  output [15:0] out_41,
  output out_42,
  output out_43,
  output out_44,
  output out_45,
  output [15:0] out_46,
  output out_47,
  output [15:0] out_48,
  output [2:0] out_49,
  output [15:0] out_50,
  output out_51,
  output [15:0] out_52,
  output out_53,
  output out_54,
  output out_55,
  output [15:0] out_56,
  output out_57,
  output out_58
);

  wire clock_1_clock, cpu_1_out_10, cpu_1_out_14, cpu_1_out_61, RESET, SIM_ONLY_RESET, SINGLE_STEP_ADVANCE;
  wire [15:0] DATA;

  Button button_1 (.out(SIM_ONLY_RESET));
  Button button_2 (.out(RESET));
  Button button_3 (.out(SINGLE_STEP_ADVANCE));
  LED led_1 (.in(out_3));
  LED led_2 (.in(out_5));
  LED led_3 (.in(out_7));
  LED led_4 (.in(out_10));
  LED led_5 (.in(out_12));
  LED led_6 (.in(out_14));
  LED led_7 (.in(out_17));
  LED led_8 (.in(out_19));
  LED led_9 (.in(out_24));
  LED led_10 (.in(out_27));
  LED led_11 (.in(out_29));
  LED led_12 (.in(out_33));
  LED led_13 (.in(out_35));
  LED led_14 (.in(out_38));
  LED led_15 (.in(out_40));
  LED led_16 (.in(out_43));
  LED led_17 (.in(out_44));
  LED led_18 (.in(out_47));
  LED led_19 (.in(out_4));
  LED led_20 (.in(out_8));
  LED led_21 (.in(out_11));
  LED led_22 (.in(out_15));
  LED led_23 (.in(out_20));
  LED led_24 (.in(out_25));
  LED led_25 (.in(out_28));
  LED led_26 (.in(out_31));
  LED led_27 (.in(out_37));
  LED led_28 (.in(out_42));
  LED led_29 (.in(out_45));
  Clock clock_1 (.enable(in_1), .Arduino_Crystal(in_2), .Arduino_clock(SINGLE_STEP_ADVANCE), .clock(clock_1_clock));
  DotMatrix #(.matrixcols(16), .matrixrows(1)) dotmatrix_1 (
    .col0(out_9[15]), .col1(out_9[14]), .col2(out_9[13]), .col3(out_9[12]), .col4(out_9[11]),
    .col5(out_9[10]), .col6(out_9[9]), .col7(out_9[8]), .col8(out_9[7]), .col9(out_9[6]), .col10(out_9[5]),
    .col11(out_9[4]), .col12(out_9[3]), .col13(out_9[2]), .col14(out_9[1]), .col15(out_9[0]));
  DotMatrix #(.matrixcols(16), .matrixrows(1)) dotmatrix_2 (
    .col0(out_16[15]), .col1(out_16[14]), .col2(out_16[13]), .col3(out_16[12]), .col4(out_16[11]),
    .col5(out_16[10]), .col6(out_16[9]), .col7(out_16[8]), .col8(out_16[7]), .col9(out_16[6]),
    .col10(out_16[5]), .col11(out_16[4]), .col12(out_16[3]), .col13(out_16[2]), .col14(out_16[1]),
    .col15(out_16[0]));
  DotMatrix #(.matrixcols(16), .matrixrows(1)) dotmatrix_3 (
    .col0(out_22[15]), .col1(out_22[14]), .col2(out_22[13]), .col3(out_22[12]), .col4(out_22[11]),
    .col5(out_22[10]), .col6(out_22[9]), .col7(out_22[8]), .col8(out_22[7]), .col9(out_22[6]),
    .col10(out_22[5]), .col11(out_22[4]), .col12(out_22[3]), .col13(out_22[2]), .col14(out_22[1]),
    .col15(out_22[0]));
  DotMatrix #(.matrixcols(16), .matrixrows(1)) dotmatrix_4 (
    .col0(out_32[15]), .col1(out_32[14]), .col2(out_32[13]), .col3(out_32[12]), .col4(out_32[11]),
    .col5(out_32[10]), .col6(out_32[9]), .col7(out_32[8]), .col8(out_32[7]), .col9(out_32[6]),
    .col10(out_32[5]), .col11(out_32[4]), .col12(out_32[3]), .col13(out_32[2]), .col14(out_32[1]),
    .col15(out_32[0]));
  DotMatrix #(.matrixcols(16), .matrixrows(1)) dotmatrix_5 (
    .col0(out_41[15]), .col1(out_41[14]), .col2(out_41[13]), .col3(out_41[12]), .col4(out_41[11]),
    .col5(out_41[10]), .col6(out_41[9]), .col7(out_41[8]), .col8(out_41[7]), .col9(out_41[6]),
    .col10(out_41[5]), .col11(out_41[4]), .col12(out_41[3]), .col13(out_41[2]), .col14(out_41[1]),
    .col15(out_41[0]));
  DotMatrix #(.matrixcols(16), .matrixrows(1)) dotmatrix_6 (
    .col0(out_48[15]), .col1(out_48[14]), .col2(out_48[13]), .col3(out_48[12]), .col4(out_48[11]),
    .col5(out_48[10]), .col6(out_48[9]), .col7(out_48[8]), .col8(out_48[7]), .col9(out_48[6]),
    .col10(out_48[5]), .col11(out_48[4]), .col12(out_48[3]), .col13(out_48[2]), .col14(out_48[1]),
    .col15(out_48[0]));
  DotMatrix #(.matrixcols(16), .matrixrows(1)) dotmatrix_7 (
    .col0(out_50[15]), .col1(out_50[14]), .col2(out_50[13]), .col3(out_50[12]), .col4(out_50[11]),
    .col5(out_50[10]), .col6(out_50[9]), .col7(out_50[8]), .col8(out_50[7]), .col9(out_50[6]),
    .col10(out_50[5]), .col11(out_50[4]), .col12(out_50[3]), .col13(out_50[2]), .col14(out_50[1]),
    .col15(out_50[0]));
  DotMatrix #(.matrixcols(16), .matrixrows(1)) dotmatrix_8 (
    .col0(out_52[15]), .col1(out_52[14]), .col2(out_52[13]), .col3(out_52[12]), .col4(out_52[11]),
    .col5(out_52[10]), .col6(out_52[9]), .col7(out_52[8]), .col8(out_52[7]), .col9(out_52[6]),
    .col10(out_52[5]), .col11(out_52[4]), .col12(out_52[3]), .col13(out_52[2]), .col14(out_52[1]),
    .col15(out_52[0]));
  DotMatrix #(.matrixcols(16), .matrixrows(1)) dotmatrix_9 (
    .col0(out_56[15]), .col1(out_56[14]), .col2(out_56[13]), .col3(out_56[12]), .col4(out_56[11]),
    .col5(out_56[10]), .col6(out_56[9]), .col7(out_56[8]), .col8(out_56[7]), .col9(out_56[6]),
    .col10(out_56[5]), .col11(out_56[4]), .col12(out_56[3]), .col13(out_56[2]), .col14(out_56[1]),
    .col15(out_56[0]));
  // Probe on out_9
  // Probe on out_16
  // Probe on out_22
  // Probe on out_32
  // Probe on out_41
  // Probe on out_48
  // Probe on out_50
  // Probe on out_52
  // Probe on out_56
  CPU cpu_1 (
    .out_7(out_6), .out_11(out_9), .out_16(out_13), .out_19(out_16), .out_25(out_22), .out_35(out_32),
    .out_44(out_41), .out_49(out_46), .out_51(out_48), .out_52(out_49), .in_1(RESET), .out_53(out_50),
    .in_2(clock_1_clock), .out_55(out_52), .DATA_2(DATA), .out_4(out_3), .out_5(out_4), .out_6(out_5),
    .out_8(out_7), .out_9(out_8), .out_12(out_10), .out_13(out_11), .out_15(out_12), .out_17(out_14),
    .out_20(out_17), .out_18(out_15), .out_22(out_19), .out_23(out_20), .out_21(out_18), .out_24(out_21),
    .out_27(out_24), .out_28(out_25), .out_26(out_23), .out_30(out_27), .out_31(out_28), .out_29(out_26),
    .out_32(out_29), .out_34(out_31), .out_33(out_30), .out_36(out_33), .out_37(out_34), .out_38(out_35),
    .out_40(out_37), .out_39(out_36), .out_41(out_38), .out_42(out_39), .out_43(out_40), .out_45(out_42),
    .out_46(out_43), .out_47(out_44), .out_48(out_45), .out_50(out_47), .out_54(out_51), .out_56(out_53),
    .out_57(out_54), .out_58(out_55), .out_60(out_57), .out_62(out_58), .DATA(DATA), .out_59(out_56),
    .out_61(cpu_1_out_61), .out_10(cpu_1_out_10), .out_14(cpu_1_out_14));
  // Probe on out_9
  // Probe on out_9
  // Probe on out_16
  // Probe on out_16
  // Probe on out_22
  // Probe on out_22
  // Probe on out_32
  // Probe on out_32
  // Probe on out_41
  // Probe on out_41
  // Probe on out_48
  // Probe on out_48
  // Probe on out_50
  // Probe on out_50
  // Probe on out_52
  // Probe on out_52
  // Probe on out_56
  // Probe on out_56
  RAM ram_1 (
    .data_in(DATA), .address(out_56), .output_enable(cpu_1_out_14), .input_enable(cpu_1_out_10),
    .clock(cpu_1_out_61), .tristate_data_out(DATA), .chip_enable(1'b1));  // open: addressed_value
  DotMatrix #(.matrixcols(16), .matrixrows(1)) dotmatrix_10 (
    .col0(out_6[15]), .col1(out_6[14]), .col2(out_6[13]), .col3(out_6[12]), .col4(out_6[11]),
    .col5(out_6[10]), .col6(out_6[9]), .col7(out_6[8]), .col8(out_6[7]), .col9(out_6[6]), .col10(out_6[5]),
    .col11(out_6[4]), .col12(out_6[3]), .col13(out_6[2]), .col14(out_6[1]), .col15(out_6[0]));
  DotMatrix #(.matrixcols(16), .matrixrows(1)) dotmatrix_11 (
    .col0(out_13[15]), .col1(out_13[14]), .col2(out_13[13]), .col3(out_13[12]), .col4(out_13[11]),
    .col5(out_13[10]), .col6(out_13[9]), .col7(out_13[8]), .col8(out_13[7]), .col9(out_13[6]),
    .col10(out_13[5]), .col11(out_13[4]), .col12(out_13[3]), .col13(out_13[2]), .col14(out_13[1]),
    .col15(out_13[0]));
  DotMatrix #(.matrixcols(16), .matrixrows(1)) dotmatrix_12 (
    .col0(out_46[15]), .col1(out_46[14]), .col2(out_46[13]), .col3(out_46[12]), .col4(out_46[11]),
    .col5(out_46[10]), .col6(out_46[9]), .col7(out_46[8]), .col8(out_46[7]), .col9(out_46[6]),
    .col10(out_46[5]), .col11(out_46[4]), .col12(out_46[3]), .col13(out_46[2]), .col14(out_46[1]),
    .col15(out_46[0]));
  LED led_30 (.in(out_49[2]));
  LED led_31 (.in(out_51));
  LED led_32 (.in(out_53));
  LED led_33 (.in(out_54));
  LED led_34 (.in(out_55));
  LED led_35 (.in(out_57));
  LED led_36 (.in(out_58));
  LED led_37 (.in(out_18));
  LED led_38 (.in(out_21));
  LED led_39 (.in(out_23));
  LED led_40 (.in(out_26));
  LED led_41 (.in(out_30));
  LED led_42 (.in(out_34));
  LED led_43 (.in(out_36));
  LED led_44 (.in(out_39));
  LED led_45 (.in(out_49[1]));
  LED led_46 (.in(out_49[0]));
  // Probe on out_6
  // Probe on out_6
  // Probe on out_6
  // Probe on out_13
  // Probe on out_13
  // Probe on out_13
  // Probe on out_46
  // Probe on out_46
  // Probe on out_46
  // Probe on out_49
  // Probe on out_49
  // Probe on out_49

  // Other names for the same wires on the sheet: A[15:0] = out_48; A_IN = out_7; A_OUT = out_10; ACC[15:0] = out_41;
  //   ACC_IN = out_3; ACC_OUT = out_5; ADDRESS[15:0] = out_56; ALU_A_IS_BUS = out_33; ALU_C_IN = out_47;
  //   ALU_CARRYBORROW_FLAG_CLOCKED = out_36; ALU_CARRYBORROW_FLAG_IMM = out_23; ALU_EQUAL_FLAG_CLOCKED = out_39;
  //   ALU_EQUAL_FLAG_IMM = out_26; ALU_M = out_44; ALU_NEGATIVE_FLAG_CLOCKED = out_34; ALU_NEGATIVE_FLAG_IMM = out_21;
  //   ALU_OUT = out_29; ALU_RESULT_CLOCKED[15:0] = out_13; ALU_RESULT_IMM[15:0] = out_6; ALU_S0 = out_35;
  //   ALU_S1 = out_38; ALU_S2 = out_40; ALU_S3 = out_43; ALU_STORE_FLAGS = out_27; ALU_STORE_RESULT = out_24;
  //   ALU_ZERO_FLAG_CLOCKED = out_30; ALU_ZERO_FLAG_IMM = out_18; B[15:0] = out_50; B_IN = out_12; B_OUT = out_14;
  //   BUS[15:0] = out_9; C[15:0] = out_52; C_IN = out_17; C_OUT = out_19; CLOCK_ENABLE = in_1; CLOCK_HALT = out_45;
  //   CONTROL_CLOCK = out_58; CU_CARRYBORROW_MIRROR = out_54; CU_EQUAL_MIRROR = out_55;
  //   CU_INSTRUCTION_MIRROR[15:0] = out_46; CU_MICROCODE_STEP[2:0] = out_49; CU_NEGATIVE_MIRROR = out_53;
  //   CU_STEP_RESET = out_42; CU_ZERO_MIRROR = out_51; DATA_CLOCK = out_57; EXTERNAL_INTERNAL_CLOCK = in_2;
  //   IR[15:0] = out_22; IR_IN = out_37; MAR_IN = out_4; PC[15:0] = out_16; PC_COUNT = out_31; PC_IN = out_25;
  //   PC_OUT = out_28; READ_FROM_MEM = out_11; SP[15:0] = out_32; SP_IN = out_15; SP_OUT = out_20;
  //   WRITE_TO_MEM = out_8

  // Notes on the sheet:
  //   BIN
  //   HEX
  //   DEC
  //   BIN
  //   HEX
  //   DEC
  //   BIN
  //   HEX
  //   DEC
  //   BIN
  //   HEX
  //   DEC
  //   BIN
  //   HEX
  //   DEC
  //   BIN
  //   HEX
  //   DEC
  //   BIN
  //   HEX
  //   DEC
  //   BIN
  //   HEX
  //   DEC
  //   BIN
  //   HEX
  //   DEC
  //   BIN
  //   HEX
  //   DEC
  //   BIN
  //   HEX
  //   DEC
  //   BIN
  //   HEX
  //   DEC
  //   BIN
  //   HEX
  //   DEC
endmodule

module CPU (
  input  in_1,
  input  in_2,
  input  [15:0] DATA,
  output out_4,
  output out_5,
  output out_6,
  output [15:0] out_7,
  output out_8,
  output out_9,
  output out_10,
  output [15:0] out_11,
  output out_12,
  output out_13,
  output out_14,
  output out_15,
  output [15:0] out_16,
  output out_17,
  output out_18,
  output [15:0] out_19,
  output out_20,
  output out_21,
  output out_22,
  output out_23,
  output out_24,
  output [15:0] out_25,
  output out_26,
  output out_27,
  output out_28,
  output out_29,
  output out_30,
  output out_31,
  output out_32,
  output out_33,
  output out_34,
  output [15:0] out_35,
  output out_36,
  output out_37,
  output out_38,
  output out_39,
  output out_40,
  output out_41,
  output out_42,
  output out_43,
  output [15:0] out_44,
  output out_45,
  output out_46,
  output out_47,
  output out_48,
  output [15:0] out_49,
  output out_50,
  output [15:0] out_51,
  output [2:0] out_52,
  output [15:0] out_53,
  output out_54,
  output [15:0] out_55,
  output out_56,
  output out_57,
  output out_58,
  output [15:0] out_59,
  output out_60,
  output out_61,
  output out_62,
  output [15:0] DATA_2
);

  wire j_k_ff_1_q, j_k_ff_1_qn, nor_1_out, safe_clock_enable_1_clock_out, SIM_ONLY_RESET;
  wire [15:0] multiplexer_1_out;

  Button button_1 (.out(SIM_ONLY_RESET));
  LED led_1 (.in(out_4));
  LED led_2 (.in(out_6));
  LED led_3 (.in(out_8));
  LED led_4 (.in(out_12));
  LED led_5 (.in(out_15));
  LED led_6 (.in(out_17));
  LED led_7 (.in(out_20));
  LED led_8 (.in(out_22));
  LED led_9 (.in(out_27));
  LED led_10 (.in(out_30));
  LED led_11 (.in(out_32));
  LED led_12 (.in(out_36));
  LED led_13 (.in(out_38));
  LED led_14 (.in(out_41));
  LED led_15 (.in(out_43));
  LED led_16 (.in(out_46));
  LED led_17 (.in(out_47));
  LED led_18 (.in(out_50));
  nor nor_1 (nor_1_out, in_1, out_48);
  LED led_19 (.in(out_5));
  LED led_20 (.in(out_9));
  LED led_21 (.in(out_13));
  LED led_22 (.in(out_18));
  LED led_23 (.in(out_23));
  LED led_24 (.in(out_28));
  LED led_25 (.in(out_31));
  LED led_26 (.in(out_34));
  LED led_27 (.in(out_40));
  LED led_28 (.in(out_45));
  LED led_29 (.in(out_48));
  safe_clock_enable safe_clock_enable_1 (
    .clock_enable(nor_1_out), .clock_in(in_2), .clock_out(safe_clock_enable_1_clock_out));
  J_K_Flip_Flop j_k_ff_1 (
    .J(1'b1), .clk(safe_clock_enable_1_clock_out), .K(1'b1), .Q(j_k_ff_1_q), .Qn(j_k_ff_1_qn), .preset(1'b0),
    .en(1'b1), .reset(in_1));
  DotMatrix #(.matrixcols(16), .matrixrows(1)) dotmatrix_1 (
    .col0(out_11[15]), .col1(out_11[14]), .col2(out_11[13]), .col3(out_11[12]), .col4(out_11[11]),
    .col5(out_11[10]), .col6(out_11[9]), .col7(out_11[8]), .col8(out_11[7]), .col9(out_11[6]),
    .col10(out_11[5]), .col11(out_11[4]), .col12(out_11[3]), .col13(out_11[2]), .col14(out_11[1]),
    .col15(out_11[0]));
  DotMatrix #(.matrixcols(16), .matrixrows(1)) dotmatrix_2 (
    .col0(out_19[15]), .col1(out_19[14]), .col2(out_19[13]), .col3(out_19[12]), .col4(out_19[11]),
    .col5(out_19[10]), .col6(out_19[9]), .col7(out_19[8]), .col8(out_19[7]), .col9(out_19[6]),
    .col10(out_19[5]), .col11(out_19[4]), .col12(out_19[3]), .col13(out_19[2]), .col14(out_19[1]),
    .col15(out_19[0]));
  DotMatrix #(.matrixcols(16), .matrixrows(1)) dotmatrix_3 (
    .col0(out_25[15]), .col1(out_25[14]), .col2(out_25[13]), .col3(out_25[12]), .col4(out_25[11]),
    .col5(out_25[10]), .col6(out_25[9]), .col7(out_25[8]), .col8(out_25[7]), .col9(out_25[6]),
    .col10(out_25[5]), .col11(out_25[4]), .col12(out_25[3]), .col13(out_25[2]), .col14(out_25[1]),
    .col15(out_25[0]));
  DotMatrix #(.matrixcols(16), .matrixrows(1)) dotmatrix_4 (
    .col0(out_35[15]), .col1(out_35[14]), .col2(out_35[13]), .col3(out_35[12]), .col4(out_35[11]),
    .col5(out_35[10]), .col6(out_35[9]), .col7(out_35[8]), .col8(out_35[7]), .col9(out_35[6]),
    .col10(out_35[5]), .col11(out_35[4]), .col12(out_35[3]), .col13(out_35[2]), .col14(out_35[1]),
    .col15(out_35[0]));
  DotMatrix #(.matrixcols(16), .matrixrows(1)) dotmatrix_5 (
    .col0(out_44[15]), .col1(out_44[14]), .col2(out_44[13]), .col3(out_44[12]), .col4(out_44[11]),
    .col5(out_44[10]), .col6(out_44[9]), .col7(out_44[8]), .col8(out_44[7]), .col9(out_44[6]),
    .col10(out_44[5]), .col11(out_44[4]), .col12(out_44[3]), .col13(out_44[2]), .col14(out_44[1]),
    .col15(out_44[0]));
  DotMatrix #(.matrixcols(16), .matrixrows(1)) dotmatrix_6 (
    .col0(out_51[15]), .col1(out_51[14]), .col2(out_51[13]), .col3(out_51[12]), .col4(out_51[11]),
    .col5(out_51[10]), .col6(out_51[9]), .col7(out_51[8]), .col8(out_51[7]), .col9(out_51[6]),
    .col10(out_51[5]), .col11(out_51[4]), .col12(out_51[3]), .col13(out_51[2]), .col14(out_51[1]),
    .col15(out_51[0]));
  DotMatrix #(.matrixcols(16), .matrixrows(1)) dotmatrix_7 (
    .col0(out_53[15]), .col1(out_53[14]), .col2(out_53[13]), .col3(out_53[12]), .col4(out_53[11]),
    .col5(out_53[10]), .col6(out_53[9]), .col7(out_53[8]), .col8(out_53[7]), .col9(out_53[6]),
    .col10(out_53[5]), .col11(out_53[4]), .col12(out_53[3]), .col13(out_53[2]), .col14(out_53[1]),
    .col15(out_53[0]));
  DotMatrix #(.matrixcols(16), .matrixrows(1)) dotmatrix_8 (
    .col0(out_55[15]), .col1(out_55[14]), .col2(out_55[13]), .col3(out_55[12]), .col4(out_55[11]),
    .col5(out_55[10]), .col6(out_55[9]), .col7(out_55[8]), .col8(out_55[7]), .col9(out_55[6]),
    .col10(out_55[5]), .col11(out_55[4]), .col12(out_55[3]), .col13(out_55[2]), .col14(out_55[1]),
    .col15(out_55[0]));
  DotMatrix #(.matrixcols(16), .matrixrows(1)) dotmatrix_9 (
    .col0(out_59[15]), .col1(out_59[14]), .col2(out_59[13]), .col3(out_59[12]), .col4(out_59[11]),
    .col5(out_59[10]), .col6(out_59[9]), .col7(out_59[8]), .col8(out_59[7]), .col9(out_59[6]),
    .col10(out_59[5]), .col11(out_59[4]), .col12(out_59[3]), .col13(out_59[2]), .col14(out_59[1]),
    .col15(out_59[0]));
  control_unit control_unit_1 (
    .mirror_instruction(out_49), .instruction(out_25), .equal_flag(out_42), .carryborrow_flag(out_39),
    .negative_flag(out_37), .zero_flag(out_33), .mirror_equal_flag(out_58), .mirror_carryborrow_flag(out_57),
    .mirror_negative_flag(out_56), .mirror_zero_flag(out_54), .microcode_step(out_52),
    .control_clock(out_62), .reset(in_1), .sim_only_clear(SIM_ONLY_RESET), .CLOCK_HALT(out_48),
    .CU_STEP_RESET(out_45), .IR_IN(out_40), .PC_COUNT(out_34), .PC_OUT(out_31), .PC_IN(out_28),
    .SP_OUT(out_23), .SP_IN(out_18), .READ_FROM_MEM(out_13), .WRITE_TO_MEM(out_9), .MAR_IN(out_5),
    .ALU_C_IN(out_50), .ALU_M(out_47), .ALU_S3(out_46), .ALU_S2(out_43), .ALU_S1(out_41), .ALU_S0(out_38),
    .ALU_A_IS_BUS(out_36), .ALU_OUT(out_32), .ALU_STORE_FLAGS(out_30), .ALU_STORE_RESULT(out_27),
    .C_OUT(out_22), .C_IN(out_20), .B_OUT(out_17), .B_IN(out_15), .A_OUT(out_12), .A_IN(out_8),
    .ACC_OUT(out_6), .ACC_IN(out_4));
  register_bus_R register_bus_r_1 (
    .\input (out_11), .input_enable(out_40), .clock(out_60), .buffered_output(out_11), .content(out_25),
    .sim_only_reset(SIM_ONLY_RESET), .output_enable(1'b0));
  register_bus_R register_bus_r_2 (
    .\input (out_11), .input_enable(out_5), .clock(out_60), .content(out_59),
    .sim_only_reset(SIM_ONLY_RESET), .output_enable(1'b0));  // open: buffered_output
  J_K_Flip_Flop j_k_ff_2 (
    .J(1'b1), .clk(j_k_ff_1_q), .K(1'b1), .Q(out_60), .preset(1'b0), .en(1'b1), .reset(in_1));  // open: Qn
  // Probe on out_11
  // Probe on out_19
  // Probe on out_25
  // Probe on out_35
  // Probe on out_44
  // Probe on out_51
  // Probe on out_53
  // Probe on out_55
  // Probe on out_59
  // Probe on out_11
  // Probe on out_11
  // Probe on out_19
  // Probe on out_19
  // Probe on out_25
  // Probe on out_25
  // Probe on out_35
  // Probe on out_35
  // Probe on out_44
  // Probe on out_44
  // Probe on out_51
  // Probe on out_51
  // Probe on out_53
  // Probe on out_53
  // Probe on out_55
  // Probe on out_55
  // Probe on out_59
  // Probe on out_59
  J_K_Flip_Flop j_k_ff_3 (
    .J(1'b1), .clk(j_k_ff_1_qn), .K(1'b1), .Q(out_62), .preset(1'b0), .en(1'b1), .reset(in_1));  // open: Qn
  assign DATA_2 = out_9 ? out_11 : 16'bz;  // Controlled_Buffer controlled_buffer_1
  assign out_11 = out_13 ? DATA : 16'bz;  // Controlled_Buffer controlled_buffer_2
  DotMatrix #(.matrixcols(16), .matrixrows(1)) dotmatrix_10 (
    .col0(out_7[15]), .col1(out_7[14]), .col2(out_7[13]), .col3(out_7[12]), .col4(out_7[11]),
    .col5(out_7[10]), .col6(out_7[9]), .col7(out_7[8]), .col8(out_7[7]), .col9(out_7[6]), .col10(out_7[5]),
    .col11(out_7[4]), .col12(out_7[3]), .col13(out_7[2]), .col14(out_7[1]), .col15(out_7[0]));
  DotMatrix #(.matrixcols(16), .matrixrows(1)) dotmatrix_11 (
    .col0(out_16[15]), .col1(out_16[14]), .col2(out_16[13]), .col3(out_16[12]), .col4(out_16[11]),
    .col5(out_16[10]), .col6(out_16[9]), .col7(out_16[8]), .col8(out_16[7]), .col9(out_16[6]),
    .col10(out_16[5]), .col11(out_16[4]), .col12(out_16[3]), .col13(out_16[2]), .col14(out_16[1]),
    .col15(out_16[0]));
  DotMatrix #(.matrixcols(16), .matrixrows(1)) dotmatrix_12 (
    .col0(out_49[15]), .col1(out_49[14]), .col2(out_49[13]), .col3(out_49[12]), .col4(out_49[11]),
    .col5(out_49[10]), .col6(out_49[9]), .col7(out_49[8]), .col8(out_49[7]), .col9(out_49[6]),
    .col10(out_49[5]), .col11(out_49[4]), .col12(out_49[3]), .col13(out_49[2]), .col14(out_49[1]),
    .col15(out_49[0]));
  LED led_30 (.in(out_52[2]));
  LED led_31 (.in(out_54));
  LED led_32 (.in(out_56));
  LED led_33 (.in(out_57));
  LED led_34 (.in(out_58));
  LED led_35 (.in(out_60));
  LED led_36 (.in(out_62));
  Pull_Resistor pull_resistor_1 (.node(out_11));
  LED led_37 (.in(out_21));
  LED led_38 (.in(out_24));
  LED led_39 (.in(out_26));
  LED led_40 (.in(out_29));
  LED led_41 (.in(out_33));
  LED led_42 (.in(out_37));
  LED led_43 (.in(out_39));
  LED led_44 (.in(out_42));
  LED led_45 (.in(out_52[1]));
  LED led_46 (.in(out_52[0]));
  Multiplexer #(.width(16), .enable("false")) multiplexer_1 (
    .in0(out_44), .in1(out_11), .out(multiplexer_1_out), .sel(out_36));
  ALU alu_1 (
    .carry_in(out_50), .M(out_47), .S0(out_38), .S1(out_41), .S2(out_43), .S3(out_46), .clock(out_60),
    .store_result(out_27), .store_flags(out_30), .unclocked_zero(out_21), .clocked_zero(out_33),
    .unclocked_negative(out_24), .clocked_negative(out_37), .unclocked_carryborrow_out(out_26),
    .clocked_carryborrow_out(out_39), .unclocked_A___B(out_29), .clocked_A___B(out_42),
    .tristate_clocked_result(out_11), .sim_only_reset(SIM_ONLY_RESET), .A(multiplexer_1_out), .B(out_11),
    .result_output_enable(out_32), .unclocked_result(out_7), .clocked_result(out_16));
  // Probe on out_7
  // Probe on out_7
  // Probe on out_7
  // Probe on out_16
  // Probe on out_16
  // Probe on out_16
  // Probe on out_49
  // Probe on out_49
  // Probe on out_49
  // Probe on out_52
  // Probe on out_52
  // Probe on out_52
  program_counter program_counter_1 (
    .\input (out_11), .count(out_34), .clock(out_60), .reset(in_1), .output_enable(out_31),
    .tristate_output(out_11), .contents(out_19), .in(out_28));
  register_bus_L register_bus_l_1 (
    .\input (out_11), .input_enable(out_4), .clock(out_60), .buffered_output(out_11), .content(out_44),
    .sim_only_reset(SIM_ONLY_RESET), .output_enable(out_6));
  register_bus_L register_bus_l_2 (
    .\input (out_11), .input_enable(out_8), .clock(out_60), .buffered_output(out_11), .content(out_51),
    .sim_only_reset(SIM_ONLY_RESET), .output_enable(out_12));
  register_bus_L register_bus_l_3 (
    .\input (out_11), .input_enable(out_15), .clock(out_60), .buffered_output(out_11), .content(out_53),
    .sim_only_reset(SIM_ONLY_RESET), .output_enable(out_17));
  register_bus_L register_bus_l_4 (
    .\input (out_11), .input_enable(out_20), .clock(out_60), .buffered_output(out_11), .content(out_55),
    .sim_only_reset(SIM_ONLY_RESET), .output_enable(out_22));
  register_bus_L register_bus_l_5 (
    .\input (out_11), .input_enable(out_18), .clock(out_60), .buffered_output(out_11), .content(out_35),
    .sim_only_reset(SIM_ONLY_RESET), .output_enable(out_23));

  assign out_10 = out_9;
  assign out_14 = out_13;
  assign out_61 = out_60;

  // Other names for the same wires on the sheet: A[15:0] = out_51; A_IN = out_8; A_OUT = out_12; ACC[15:0] = out_44;
  //   ACC_IN = out_4; ACC_OUT = out_6; ADDRESS[15:0] = out_59; ALU_A_IS_BUS = out_36; ALU_C_IN = out_50;
  //   ALU_CARRYBORROW_FLAG_CLOCKED = out_39; ALU_CARRYBORROW_FLAG_IMM = out_26; ALU_EQUAL_FLAG_CLOCKED = out_42;
  //   ALU_EQUAL_FLAG_IMM = out_29; ALU_M = out_47; ALU_NEGATIVE_FLAG_CLOCKED = out_37; ALU_NEGATIVE_FLAG_IMM = out_24;
  //   ALU_OUT = out_32; ALU_RESULT_CLOCKED[15:0] = out_16; ALU_RESULT_IMM[15:0] = out_7; ALU_S0 = out_38;
  //   ALU_S1 = out_41; ALU_S2 = out_43; ALU_S3 = out_46; ALU_STORE_FLAGS = out_30; ALU_STORE_RESULT = out_27;
  //   ALU_ZERO_FLAG_CLOCKED = out_33; ALU_ZERO_FLAG_IMM = out_21; B[15:0] = out_53; B_IN = out_15; B_OUT = out_17;
  //   BUS[15:0] = out_11; C[15:0] = out_55; C_IN = out_20; C_OUT = out_22; CLOCK_HALT = out_48;
  //   CONTROL_CLOCK = out_62; CU_CARRYBORROW_MIRROR = out_57; CU_EQUAL_MIRROR = out_58;
  //   CU_INSTRUCTION_MIRROR[15:0] = out_49; CU_MICROCODE_STEP[2:0] = out_52; CU_NEGATIVE_MIRROR = out_56;
  //   CU_STEP_RESET = out_45; CU_ZERO_MIRROR = out_54; DATA_CLOCK = out_60; EXT_CLOCK_PULSE = in_2; IR[15:0] = out_25;
  //   IR_IN = out_40; MAR_IN = out_5; PC[15:0] = out_19; PC_COUNT = out_34; PC_IN = out_28; PC_OUT = out_31;
  //   READ_FROM_MEM = out_13; RESET = in_1; SP[15:0] = out_35; SP_IN = out_18; SP_OUT = out_23; WRITE_TO_MEM = out_9

  // Notes on the sheet:
  //   BIN
  //   HEX
  //   DEC
  //   BIN
  //   HEX
  //   DEC
  //   BIN
  //   HEX
  //   DEC
  //   BIN
  //   HEX
  //   DEC
  //   BIN
  //   HEX
  //   DEC
  //   BIN
  //   HEX
  //   DEC
  //   BIN
  //   HEX
  //   DEC
  //   BIN
  //   HEX
  //   DEC
  //   BIN
  //   HEX
  //   DEC
  //   BIN
  //   HEX
  //   DEC
  //   BIN
  //   HEX
  //   DEC
  //   BIN
  //   HEX
  //   DEC
  //   BIN
  //   HEX
  //   DEC
endmodule

module RAM (
  input  [15:0] data_in,
  input  [15:0] address,
  input  chip_enable,
  input  output_enable,
  input  input_enable,
  input  clock,
  output [15:0] addressed_value,
  output [15:0] tristate_data_out
);

  wire multiplexer_1_out, multiplexer_2_out, not_1_out, safe_clock_enable_1_clock_out;

  Multiplexer multiplexer_1 (.in0(1'b0), .in1(input_enable), .out(multiplexer_1_out), .sel(chip_enable), .en(1'b1));
  safe_clock_enable safe_clock_enable_1 (
    .clock_enable(multiplexer_1_out), .clock_in(clock), .clock_out(safe_clock_enable_1_clock_out));
  Multiplexer multiplexer_2 (.in0(1'b0), .in1(output_enable), .out(multiplexer_2_out), .sel(chip_enable), .en(1'b1));
  RAM_part #(.addrWidth(16), .dataWidth(16)) ram_1 (
    .addr(address), .data(addressed_value), .sel(1'b1), .clk(safe_clock_enable_1_clock_out), .ld(not_1_out),
    .clr(1'b0));
  assign addressed_value = multiplexer_1_out ? data_in : 16'bz;  // Controlled_Buffer controlled_buffer_1
  not not_1 (not_1_out, multiplexer_1_out);
  assign tristate_data_out = multiplexer_2_out ? addressed_value : 16'bz;  // Controlled_Buffer controlled_buffer_2
endmodule

module control_unit (
  input  [15:0] instruction,
  input  equal_flag,
  input  carryborrow_flag,
  input  negative_flag,
  input  zero_flag,
  input  control_clock,
  input  reset,
  input  sim_only_clear,
  output [15:0] mirror_instruction,
  output CLOCK_HALT,
  output CU_STEP_RESET,
  output IR_IN,
  output PC_COUNT,
  output PC_OUT,
  output PC_IN,
  output SP_OUT,
  output SP_IN,
  output mirror_equal_flag,
  output READ_FROM_MEM,
  output mirror_carryborrow_flag,
  output WRITE_TO_MEM,
  output mirror_negative_flag,
  output MAR_IN,
  output mirror_zero_flag,
  output ALU_C_IN,
  output ALU_M,
  output [2:0] microcode_step,
  output ALU_S3,
  output ALU_S2,
  output ALU_S1,
  output ALU_S0,
  output ALU_A_IS_BUS,
  output ALU_OUT,
  output ALU_STORE_FLAGS,
  output ALU_STORE_RESULT,
  output C_OUT,
  output C_IN,
  output B_OUT,
  output B_IN,
  output A_OUT,
  output A_IN,
  output ACC_OUT,
  output ACC_IN
);

  wire not_1_out;
  wire [7:5] rom_1_data;

  not not_1 (not_1_out, CU_STEP_RESET);
  Register u_mirror_instruction (
    .D(instruction[7:0]), .en(1'b1), .Q(mirror_instruction[7:0]), .clk(control_clock), .clr(sim_only_clear));
  Register #(.width(4)) mirror_flags (
    .D({equal_flag, carryborrow_flag, negative_flag, zero_flag}), .en(1'b1),
    .Q({mirror_equal_flag, mirror_carryborrow_flag, mirror_negative_flag, mirror_zero_flag}),
    .clk(control_clock), .clr(sim_only_clear));
  Counter #(.width(3), .max('h7)) microcode_step_counter (
    .load(CU_STEP_RESET), .D(3'b000), .count(not_1_out), .Q(microcode_step), .clk(control_clock), .clr(reset));  // open: carry
  ROM #(.addrWidth(15)) rom_1 (
    .addr({mirror_instruction[7:0], mirror_equal_flag, mirror_carryborrow_flag, mirror_negative_flag, mirror_zero_flag, microcode_step}),
    .data({rom_1_data, CLOCK_HALT, CU_STEP_RESET, IR_IN, PC_COUNT, PC_OUT}), .sel(1'b1));
  ROM #(.addrWidth(15)) rom_2 (
    .addr({mirror_instruction[7:0], mirror_equal_flag, mirror_carryborrow_flag, mirror_negative_flag, mirror_zero_flag, microcode_step}),
    .data({PC_IN, SP_OUT, SP_IN, READ_FROM_MEM, WRITE_TO_MEM, MAR_IN, ALU_C_IN, ALU_M}), .sel(1'b1));
  ROM #(.addrWidth(15)) rom_3 (
    .addr({mirror_instruction[7:0], mirror_equal_flag, mirror_carryborrow_flag, mirror_negative_flag, mirror_zero_flag, microcode_step}),
    .data({ALU_S3, ALU_S2, ALU_S1, ALU_S0, ALU_A_IS_BUS, ALU_OUT, ALU_STORE_FLAGS, ALU_STORE_RESULT}),
    .sel(1'b1));
  ROM #(.addrWidth(15)) rom_4 (
    .addr({mirror_instruction[7:0], mirror_equal_flag, mirror_carryborrow_flag, mirror_negative_flag, mirror_zero_flag, microcode_step}),
    .data({C_OUT, C_IN, B_OUT, B_IN, A_OUT, A_IN, ACC_OUT, ACC_IN}), .sel(1'b1));

  assign mirror_instruction[15:8] = {8{1'b0}};

  // Notes on the sheet:
  //   Common inputs to all EEPROMS
  //   microcode 3
  //   microcode 2
  //   microcode 1
  //   microcode 0
  //   contents of rom_1 (hex, n*v repeats v):
  //   1 6 0 8 4*0 1 6 0 8 4*0 1 6 0 8 4*0 1 6 0 8 4*0 1 6 0 8 4*0 1 6 0 8 4*0 1 6 0 8 4*0 1 6 0 8 4*0 1 6
  //   0 8 4*0 1 6 0 8 4*0 1 6 0 8 4*0 1 6 0 8 4*0 1 6 0 8 4*0 1 6 0 8 4*0 1 6 0 8 4*0 1 6 0 8 4*0 1 6 0 8
  //   4*0 1 6 0 8 4*0 1 6 0 8 4*0 1 6 0 8 4*0 1 6 0 8 4*0 1 6 0 8 4*0 1 6 0 8 4*0 1 6 0 8 4*0 1 6 0 8 4*0
  //   1 6 0 8 4*0 1 6 0 8 4*0 1 6 0 8 4*0 1 6 0 8 4*0 1 6 0 8 4*0 1 6 0 8 4*0 1 6 0 8 4*0 1 6 0 8 4*0 1 6
  //   0 8 4*0 1 6 0 8 4*0 1 6 0 8 4*0 1 6 0 8 4*0 1 6 0 8 4*0 1 6 0 8 4*0 1 6 0 8 4*0 1 6 0 8 4*0 1 6 0 8
  //   4*0 1 6 0 8 4*0 1 6 0 8 4*0 1 6 0 8 4*0 1 6 0 8 4*0 1 6 0 8 4*0 1 6 0 8 4*0 1 6 1 2 8 0 0 0 1 6 1 2
  //   8 0 0 0 1 6 1 2 8 0 0 0 1 6 1 2 8 0 0 0 1 6 1 2 8 0 0 0 1 6 1 2 8 0 0 0 1 6 1 2 8 0 0 0 1 6 1 2 8 0
  //   0 0 1 6 1 2 8 0 0 0 1 6 1 2 8 0 0 0 1 6 1 2 8 0 0 0 1 6 1 2 8 0 0 0 1 6 1 2 8 0 0 0 1 6 1 2 8 0 0 0
  //   1 6 1 2 8 0 0 0 1 6 1 2 8 0 0 0 1 6 1 2 0 0 8 0 1 6 1 2 0 0 8 0 1 6 1 2 0 0 8 0 1 6 1 2 0 0 8 0 1 6
  //   1 2 0 0 8 0 1 6 1 2 0 0 8 0 1 6 1 2 0 0 8 0 1 6 1 2 0 0 8 0 1 6 1 2 0 0 8 0 1 6 1 2 0 0 8 0 1 6 1 2
  //   0 0 8 0 1 6 1 2 0 0 8 0 1 6 1 2 0 0 8 0 1 6 1 2 0 0 8 0 1 6 1 2 0 0 8 0 1 6 1 2 0 0 8 0 1 6 0 8 4*0
  //   1 6 0 8 4*0 1 6 0 8 4*0 1 6 0 8 4*0 1 6 0 8 4*0 1 6 0 8 4*0 1 6 0 8 4*0 1 6 0 8 4*0 1 6 0 8 4*0 1 6
  //   0 8 4*0 1 6 0 8 4*0 1 6 0 8 4*0 1 6 0 8 4*0 1 6 0 8 4*0 1 6 0 8 4*0 1 6 0 8 4*0 1 6 0 8 4*0 1 6 0 8
  //   4*0 1 6 0 8 4*0 1 6 0 8 4*0 1 6 0 8 4*0 1 6 0 8 4*0 1 6 0 8 4*0 1 6 0 8 4*0 1 6 0 8 4*0 1 6 0 8 4*0
  //   1 6 0 8 4*0 1 6 0 8 4*0 1 6 0 8 4*0 1 6 0 8 4*0 1 6 0 8 4*0 1 6 0 8 4*0 1 6 0 8 4*0 1 6 0 8 4*0 1 6
  //   0 8 4*0 1 6 0 8 4*0 1 6 0 8 4*0 1 6 0 8 4*0 1 6 0 8 4*0 1 6 0 8 4*0 1 6 0 8 4*0 1 6 0 8 4*0 1 6 0 8
  //   4*0 1 6 0 8 4*0 1 6 0 8 4*0 1 6 0 8 4*0 1 6 0 8 4*0 1 6 0 8 4*0 1 6 1 2 8 0 0 0 1 6 1 2 8 0 0 0 1 6
  //   1 2 8 0 0 0 1 6 1 2 8 0 0 0 1 6 1 2 8 0 0 0 1 6 1 2 8 0 0 0 1 6 1 2 8 0 0 0 1 6 1 2 8 0 0 0 1 6 1 2
  //   8 0 0 0 1 6 1 2 8 0 0 0 1 6 1 2 8 0 0 0 1 6 1 2 8 0 0 0 1 6 1 2 8 0 0 0 1 6 1 2 8 0 0 0 1 6 1 2 8 0
  //   0 0 1 6 1 2 8 0 0 0 1 6 1 2 0 0 8 0 1 6 1 2 0 0 8 0 1 6 1 2 0 0 8 0 1 6 1 2 0 0 8 0 1 6 1 2 0 0 8 0
  //   1 6 1 2 0 0 8 0 1 6 1 2 0 0 8 0 1 6 1 2 0 0 8 0 1 6 1 2 0 0 8 0 1 6 1 2 0 0 8 0 1 6 1 2 0 0 8 0 1 6
  //   1 2 0 0 8 0 1 6 1 2 0 0 8 0 1 6 1 2 0 0 8 0 1 6 1 2 0 0 8 0 1 6 1 2 0 0 8 0 1 6 0 8 4*0 1 6 0 8 4*0
  //   1 6 0 8 4*0 1 6 0 8 4*0 1 6 0 8 4*0 1 6 0 8 4*0 1 6 0 8 4*0 1 6 0 8 4*0 1 6 0 8 4*0 1 6 0 8 4*0 1 6
  //   0 8 4*0 1 6 0 8 4*0 1 6 0 8 4*0 1 6 0 8 4*0 1 6 0 8 4*0 1 6 0 8 4*0 1 6 0 8 4*0 1 6 0 8 4*0 1 6 0 8
  //   4*0 1 6 0 8 4*0 1 6 0 8 4*0 1 6 0 8 4*0 1 6 0 8 4*0 1 6 0 8 4*0 1 6 0 8 4*0 1 6 0 8 4*0 1 6 0 8 4*0
  //   1 6 0 8 4*0 1 6 0 8 4*0 1 6 0 8 4*0 1 6 0 8 4*0 1 6 0 8 4*0 1 6 0 8 4*0 1 6 0 8 4*0 1 6 0 8 4*0 1 6
  //   0 8 4*0 1 6 0 8 4*0 1 6 0 8 4*0 1 6 0 8 4*0 1 6 0 8 4*0 1 6 0 8 4*0 1 6 0 8 4*0 1 6 0 8 4*0 1 6 0 8
  //   4*0 1 6 0 8 4*0 1 6 0 8 4*0 1 6 0 8 4*0 1 6 0 8 4*0 1 6 0 8 4*0 1 6 0 8 4*0 1 6 0 8 4*0 1 6 0 8 4*0
  //   1 6 0 8 4*0 1 6 0 8 4*0 1 6 0 8 4*0 1 6 0 8 4*0 1 6 0 8 4*0 1 6 0 8 4*0 1 6 0 8 4*0 1 6 0 8 4*0 1 6
  //   0 8 4*0 1 6 0 8 4*0 1 6 0 8 4*0 1 6 0 8 4*0 1 6 0 8 4*0 1 6 0 8 4*0 1 6 0 8 4*0 1 6 0 8 4*0 1 6 0 8
  //   4*0 1 6 0 8 4*0 1 6 0 8 4*0 1 6 0 8 4*0 1 6 0 8 4*0 1 6 0 8 4*0 1 6 0 8 4*0 1 6 0 8 4*0 1 6 0 8 4*0
  //   1 6 0 8 4*0 1 6 0 8 4*0 1 6 0 8 4*0 1 6 0 8 4*0 1 6 0 8 4*0 1 6 0 8 4*0 1 6 0 8 4*0 1 6 0 8 4*0 1 6
  //   0 8 4*0 1 6 0 8 4*0 1 6 0 8 4*0 1 6 0 8 4*0 1 6 0 8 4*0 1 6 0 8 4*0 1 6 0 8 4*0 1 6 0 8 4*0 1 6 0 8
  //   4*0 1 6 0 8 4*0 1 6 0 8 4*0 1 6 0 8 4*0 1 6 0 8 4*0 1 6 0 8 4*0 1 6 0 8 4*0 1 6 0 8 4*0 1 6 0 8 4*0
  //   1 6 0 8 4*0 1 6 0 8 4*0 1 6 0 8 4*0 1 6 0 8 4*0 1 6 0 8 4*0 1 6 0 8 4*0 1 6 0 8 4*0 1 6 0 8 4*0 1 6
  //   0 8 4*0 1 6 0 8 4*0 1 6 0 8 4*0 1 6 0 8 4*0 1 6 0 8 4*0 1 6 0 8 4*0 1 6 0 8 4*0 1 6 0 8 4*0 1 6 0 8
  //   4*0 1 6 0 8 4*0 1 6 0 8 4*0 1 6 0 8 4*0 1 6 0 8 4*0 1 6 0 8 4*0 1 6 0 8 4*0 1 6 0 8 4*0 1 6 0 8 4*0
  //   1 6 0 8 4*0 1 6 0 8 4*0 1 6 0 8 4*0 1 6 0 8 4*0 1 6 0 8 4*0 1 6 0 8 4*0 1 6 0 8 4*0 1 6 0 8 4*0 1 6
  //   0 8 4*0 1 6 0 8 4*0 1 6 0 8 4*0 1 6 0 8 4*0 1 6 0 8 4*0 1 6 0 8 4*0 1 6 0 8 4*0 1 6 0 8 4*0 1 6 0 8
  //   4*0 1 6 0 8 4*0 1 6 0 8 4*0 1 6 0 8 4*0 1 6 0 8 4*0 1 6 0 8 4*0 1 6 0 8 4*0 1 6 0 8 4*0 1 6 0 8 4*0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
  //   contents of rom_2 (hex, n*v repeats v):
  //   4 10 6*0 4 10 6*0 4 10 6*0 4 10 6*0 4 10 6*0 4 10 6*0 4 10 6*0 4 10 6*0 4 10 6*0 4 10 6*0 4 10 6*0 4
  //   10 6*0 4 10 6*0 4 10 6*0 4 10 6*0 4 10 6*0 4 10 6*0 4 10 6*0 4 10 6*0 4 10 6*0 4 10 6*0 4 10 6*0 4
  //   10 6*0 4 10 6*0 4 10 6*0 4 10 6*0 4 10 6*0 4 10 6*0 4 10 6*0 4 10 6*0 4 10 6*0 4 10 6*0 4 10 6*0 4
  //   10 6*0 4 10 6*0 4 10 6*0 4 10 6*0 4 10 6*0 4 10 6*0 4 10 6*0 4 10 6*0 4 10 6*0 4 10 6*0 4 10 6*0 4
  //   10 6*0 4 10 6*0 4 10 6*0 4 10 6*0 4 10 4 10 4*0 4 10 4 10 4*0 4 10 4 10 4*0 4 10 4 10 4*0 4 10 4 10
  //   4*0 4 10 4 10 4*0 4 10 4 10 4*0 4 10 4 10 4*0 4 10 4 10 4*0 4 10 4 10 4*0 4 10 4 10 4*0 4 10 4 10
  //   4*0 4 10 4 10 4*0 4 10 4 10 4*0 4 10 4 10 4*0 4 10 4 10 4*0 4 10 4 10 4 10 0 0 4 10 4 10 4 10 0 0 4
  //   10 4 10 4 10 0 0 4 10 4 10 4 10 0 0 4 10 4 10 4 10 0 0 4 10 4 10 4 10 0 0 4 10 4 10 4 10 0 0 4 10 4
  //   10 4 10 0 0 4 10 4 10 4 10 0 0 4 10 4 10 4 10 0 0 4 10 4 10 4 10 0 0 4 10 4 10 4 10 0 0 4 10 4 10 4
  //   10 0 0 4 10 4 10 4 10 0 0 4 10 4 10 4 10 0 0 4 10 4 10 4 10 0 0 4 10 2 5*0 4 10 2 5*0 4 10 2 5*0 4
  //   10 2 5*0 4 10 2 5*0 4 10 2 5*0 4 10 2 5*0 4 10 2 5*0 4 10 2 5*0 4 10 2 5*0 4 10 2 5*0 4 10 2 5*0 4
  //   10 2 5*0 4 10 2 5*0 4 10 2 5*0 4 10 2 5*0 4 10 2 5*0 4 10 2 5*0 4 10 2 5*0 4 10 2 5*0 4 10 2 5*0 4
  //   10 2 5*0 4 10 2 5*0 4 10 2 5*0 4 10 2 5*0 4 10 2 5*0 4 10 2 5*0 4 10 2 5*0 4 10 2 5*0 4 10 2 5*0 4
  //   10 2 5*0 4 10 2 5*0 4 10 2 5*0 4 10 2 5*0 4 10 2 5*0 4 10 2 5*0 4 10 2 5*0 4 10 2 5*0 4 10 2 5*0 4
  //   10 2 5*0 4 10 2 5*0 4 10 2 5*0 4 10 2 5*0 4 10 2 5*0 4 10 2 5*0 4 10 2 5*0 4 10 2 5*0 4 10 2 5*0 4
  //   10 4 12 4*0 4 10 4 12 4*0 4 10 4 12 4*0 4 10 4 12 4*0 4 10 4 12 4*0 4 10 4 12 4*0 4 10 4 12 4*0 4 10
  //   4 12 4*0 4 10 4 12 4*0 4 10 4 12 4*0 4 10 4 12 4*0 4 10 4 12 4*0 4 10 4 12 4*0 4 10 4 12 4*0 4 10 4
  //   12 4*0 4 10 4 12 4*0 4 10 4 10 4 12 0 0 4 10 4 10 4 12 0 0 4 10 4 10 4 12 0 0 4 10 4 10 4 12 0 0 4
  //   10 4 10 4 12 0 0 4 10 4 10 4 12 0 0 4 10 4 10 4 12 0 0 4 10 4 10 4 12 0 0 4 10 4 10 4 12 0 0 4 10 4
  //   10 4 12 0 0 4 10 4 10 4 12 0 0 4 10 4 10 4 12 0 0 4 10 4 10 4 12 0 0 4 10 4 10 4 12 0 0 4 10 4 10 4
  //   12 0 0 4 10 4 10 4 12 0 0 4 10 6*0 4 10 6*0 4 10 6*0 4 10 6*0 4 10 6*0 4 10 6*0 4 10 6*0 4 10 6*0 4
  //   10 6*0 4 10 6*0 4 10 6*0 4 10 6*0 4 10 6*0 4 10 6*0 4 10 6*0 4 10 6*0 4 10 6*0 4 10 6*0 4 10 6*0 4
  //   10 6*0 4 10 6*0 4 10 6*0 4 10 6*0 4 10 6*0 4 10 6*0 4 10 6*0 4 10 6*0 4 10 6*0 4 10 6*0 4 10 6*0 4
  //   10 6*0 4 10 6*0 4 10 6*0 4 10 6*0 4 10 6*0 4 10 6*0 4 10 6*0 4 10 6*0 4 10 6*0 4 10 6*0 4 10 6*0 4
  //   10 6*0 4 10 6*0 4 10 6*0 4 10 6*0 4 10 6*0 4 10 6*0 4 10 6*0 4 10 6*0 4 10 6*0 4 10 6*0 4 10 6*0 4
  //   10 6*0 4 10 6*0 4 10 6*0 4 10 6*0 4 10 6*0 4 10 6*0 4 10 6*0 4 10 6*0 4 10 6*0 4 10 6*0 4 10 6*0 4
  //   10 6*0 4 10 2 5*0 4 10 2 5*0 4 10 2 5*0 4 10 2 5*0 4 10 2 5*0 4 10 2 5*0 4 10 2 5*0 4 10 2 5*0 4 10
  //   2 5*0 4 10 2 5*0 4 10 2 5*0 4 10 2 5*0 4 10 2 5*0 4 10 2 5*0 4 10 2 5*0 4 10 2 5*0 4 10 2 5*0 4 10 2
  //   5*0 4 10 2 5*0 4 10 2 5*0 4 10 2 5*0 4 10 2 5*0 4 10 2 5*0 4 10 2 5*0 4 10 2 5*0 4 10 2 5*0 4 10 2
  //   5*0 4 10 2 5*0 4 10 2 5*0 4 10 2 5*0 4 10 2 5*0 4 10 2 5*0 4 10 2 5*0 4 10 2 5*0 4 10 2 5*0 4 10 2
  //   5*0 4 10 2 5*0 4 10 2 5*0 4 10 2 5*0 4 10 2 5*0 4 10 2 5*0 4 10 2 5*0 4 10 2 5*0 4 10 2 5*0 4 10 2
  //   5*0 4 10 2 5*0 4 10 2 5*0 4 10 2 5*0 4 10 2 5*0 4 10 2 5*0 4 10 2 5*0 4 10 2 5*0 4 10 2 5*0 4 10 2
  //   5*0 4 10 2 5*0 4 10 2 5*0 4 10 2 5*0 4 10 2 5*0 4 10 2 5*0 4 10 2 5*0 4 10 2 5*0 4 10 2 5*0 4 10 2
  //   5*0 4 10 2 5*0 4 10 6*0 4 10 6*0 4 10 6*0 4 10 6*0 4 10 6*0 4 10 6*0 4 10 6*0 4 10 6*0 4 10 6*0 4 10
  //   6*0 4 10 6*0 4 10 6*0 4 10 6*0 4 10 6*0 4 10 6*0 4 10 6*0 4 10 6*0 4 10 6*0 4 10 6*0 4 10 6*0 4 10
  //   6*0 4 10 6*0 4 10 6*0 4 10 6*0 4 10 6*0 4 10 6*0 4 10 6*0 4 10 6*0 4 10 6*0 4 10 6*0 4 10 6*0 4 10
  //   6*0 4 10 6*0 4 10 6*0 4 10 6*0 4 10 6*0 4 10 6*0 4 10 6*0 4 10 6*0 4 10 6*0 4 10 6*0 4 10 6*0 4 10
  //   6*0 4 10 6*0 4 10 6*0 4 10 6*0 4 10 6*0 4 10 6*0 4 10 6*0 4 10 6*0 4 10 6*0 4 10 6*0 4 10 6*0 4 10
  //   6*0 4 10 6*0 4 10 6*0 4 10 6*0 4 10 6*0 4 10 6*0 4 10 6*0 4 10 6*0 4 10 6*0 4 10 6*0 4 10 6*0 4 10
  //   6*0 4 10 6*0 4 10 6*0 4 10 6*0 4 10 6*0 4 10 6*0 4 10 6*0 4 10 6*0 4 10 6*0 4 10 6*0 4 10 6*0 4 10
  //   6*0 4 10 6*0 4 10 6*0 4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
  //   contents of rom_3 (hex, n*v repeats v):
  //   0 0 93 4 6*0 93 4 6*0 93 4 6*0 93 4 6*0 93 4 6*0 93 4 6*0 93 4 6*0 93 4 6*0 93 4 6*0 93 4 6*0 93 4
  //   6*0 93 4 6*0 93 4 6*0 93 4 6*0 93 4 6*0 93 4 6*0 93 4 6*0 93 4 6*0 93 4 6*0 93 4 6*0 93 4 6*0 93 4
  //   6*0 93 4 6*0 93 4 6*0 93 4 6*0 93 4 6*0 93 4 6*0 93 4 6*0 93 4 6*0 93 4 6*0 93 4 6*0 93 4 6*0 93 4
  //   6*0 93 4 6*0 93 4 6*0 93 4 6*0 93 4 6*0 93 4 6*0 93 4 6*0 93 4 6*0 93 4 6*0 93 4 6*0 93 4 6*0 93 4
  //   6*0 93 4 6*0 93 4 6*0 93 4 6*0 93 4 7*0 93 4 6*0 93 4 6*0 93 4 6*0 93 4 6*0 93 4 6*0 93 4 6*0 93 4
  //   6*0 93 4 6*0 93 4 6*0 93 4 6*0 93 4 6*0 93 4 6*0 93 4 6*0 93 4 6*0 93 4 6*0 93 4 6*0 9 4 93 4 4*0 9
  //   4 93 4 4*0 9 4 93 4 4*0 9 4 93 4 4*0 9 4 93 4 4*0 9 4 93 4 4*0 9 4 93 4 4*0 9 4 93 4 4*0 9 4 93 4
  //   4*0 9 4 93 4 4*0 9 4 93 4 4*0 9 4 93 4 4*0 9 4 93 4 4*0 9 4 93 4 4*0 9 4 93 4 4*0 9 4 93 4 0 0 0 63
  //   4 6*0 63 4 6*0 63 4 6*0 63 4 6*0 63 4 6*0 63 4 6*0 63 4 6*0 63 4 6*0 63 4 6*0 63 4 6*0 63 4 6*0 63 4
  //   6*0 63 4 6*0 63 4 6*0 63 4 6*0 63 4 6*0 63 4 6*0 63 4 6*0 63 4 6*0 63 4 6*0 63 4 6*0 63 4 6*0 63 4
  //   6*0 63 4 6*0 63 4 6*0 63 4 6*0 63 4 6*0 63 4 6*0 63 4 6*0 63 4 6*0 63 4 6*0 63 4 6*0 63 4 6*0 63 4
  //   6*0 63 4 6*0 63 4 6*0 63 4 6*0 63 4 6*0 63 4 6*0 63 4 6*0 63 4 6*0 63 4 6*0 63 4 6*0 63 4 6*0 63 4
  //   6*0 63 4 6*0 63 4 6*0 63 4 7*0 63 4 6*0 63 4 6*0 63 4 6*0 63 4 6*0 63 4 6*0 63 4 6*0 63 4 6*0 63 4
  //   6*0 63 4 6*0 63 4 6*0 63 4 6*0 63 4 6*0 63 4 6*0 63 4 6*0 63 4 6*0 63 4 6*0 9 4 63 4 4*0 9 4 63 4
  //   4*0 9 4 63 4 4*0 9 4 63 4 4*0 9 4 63 4 4*0 9 4 63 4 4*0 9 4 63 4 4*0 9 4 63 4 4*0 9 4 63 4 4*0 9 4
  //   63 4 4*0 9 4 63 4 4*0 9 4 63 4 4*0 9 4 63 4 4*0 9 4 63 4 4*0 9 4 63 4 4*0 9 4 63 4 0 0 0 cb 4 6*0 cb
  //   4 6*0 cb 4 6*0 cb 4 6*0 cb 4 6*0 cb 4 6*0 cb 4 6*0 cb 4 6*0 cb 4 6*0 cb 4 6*0 cb 4 6*0 cb 4 6*0 cb 4
  //   6*0 cb 4 6*0 cb 4 6*0 cb 4 6*0 cb 4 6*0 cb 4 6*0 cb 4 6*0 cb 4 6*0 cb 4 6*0 cb 4 6*0 cb 4 6*0 cb 4
  //   6*0 cb 4 6*0 cb 4 6*0 cb 4 6*0 cb 4 6*0 cb 4 6*0 cb 4 6*0 cb 4 6*0 cb 4 6*0 cb 4 6*0 cb 4 6*0 cb 4
  //   6*0 cb 4 6*0 cb 4 6*0 cb 4 6*0 cb 4 6*0 cb 4 6*0 cb 4 6*0 cb 4 6*0 cb 4 6*0 cb 4 6*0 cb 4 6*0 cb 4
  //   6*0 cb 4 6*0 cb 4 6*0 cb 4 6*0 cb 4 6*0 cb 4 6*0 cb 4 6*0 cb 4 6*0 cb 4 6*0 cb 4 6*0 cb 4 6*0 cb 4
  //   6*0 cb 4 6*0 cb 4 6*0 cb 4 6*0 cb 4 6*0 cb 4 6*0 cb 4 6*0 cb 4 6*0 b 4 6*0 b 4 6*0 b 4 6*0 b 4 6*0 b
  //   4 6*0 b 4 6*0 b 4 6*0 b 4 6*0 b 4 6*0 b 4 6*0 b 4 6*0 b 4 6*0 b 4 6*0 b 4 6*0 b 4 6*0 b 4 6*0 b 4
  //   6*0 b 4 6*0 b 4 6*0 b 4 6*0 b 4 6*0 b 4 6*0 b 4 6*0 b 4 6*0 b 4 6*0 b 4 6*0 b 4 6*0 b 4 6*0 b 4 6*0
  //   b 4 6*0 b 4 6*0 b 4 6*0 b 4 6*0 b 4 6*0 b 4 6*0 b 4 6*0 b 4 6*0 b 4 6*0 b 4 6*0 b 4 6*0 b 4 6*0 b 4
  //   6*0 b 4 6*0 b 4 6*0 b 4 6*0 b 4 6*0 b 4 6*0 b 4 6*0 b 4 6*0 b 4 6*0 b 4 6*0 b 4 6*0 b 4 6*0 b 4 6*0
  //   b 4 6*0 b 4 6*0 b 4 6*0 b 4 6*0 b 4 6*0 b 4 6*0 b 4 6*0 b 4 6*0 b 4 6*0 b 4 6*0 fb 4 6*0 fb 4 6*0 fb
  //   4 6*0 fb 4 6*0 fb 4 6*0 fb 4 6*0 fb 4 6*0 fb 4 6*0 fb 4 6*0 fb 4 6*0 fb 4 6*0 fb 4 6*0 fb 4 6*0 fb 4
  //   6*0 fb 4 6*0 fb 4 6*0 fb 4 6*0 fb 4 6*0 fb 4 6*0 fb 4 6*0 fb 4 6*0 fb 4 6*0 fb 4 6*0 fb 4 6*0 fb 4
  //   6*0 fb 4 6*0 fb 4 6*0 fb 4 6*0 fb 4 6*0 fb 4 6*0 fb 4 6*0 fb 4 6*0 fb 4 6*0 fb 4 6*0 fb 4 6*0 fb 4
  //   6*0 fb 4 6*0 fb 4 6*0 fb 4 6*0 fb 4 6*0 fb 4 6*0 fb 4 6*0 fb 4 6*0 fb 4 6*0 fb 4 6*0 fb 4 6*0 fb 4
  //   6*0 fb 4 6*0 fb 4 6*0 fb 4 6*0 fb 4 6*0 fb 4 6*0 fb 4 6*0 fb 4 6*0 fb 4 6*0 fb 4 6*0 fb 4 6*0 fb 4
  //   6*0 fb 4 6*0 fb 4 6*0 fb 4 6*0 fb 4 6*0 fb 4 6*0 fb 4 5767*0 9 4 6*0 9 4 6*0 9 4 6*0 9 4 6*0 9 4 6*0
  //   9 4 6*0 9 4 6*0 9 4 6*0 9 4 6*0 9 4 6*0 9 4 6*0 9 4 6*0 9 4 6*0 9 4 6*0 9 4 6*0 9 4 6*0 9 4 6*0 9 4
  //   6*0 9 4 6*0 9 4 6*0 9 4 6*0 9 4 6*0 9 4 6*0 9 4 6*0 9 4 6*0 9 4 6*0 9 4 6*0 9 4 6*0 9 4 6*0 9 4 6*0
  //   9 4 6*0 9 4 6*0 9 4 6*0 9 4 6*0 9 4 6*0 9 4 6*0 9 4 6*0 9 4 6*0 9 4 6*0 9 4 6*0 9 4 6*0 9 4 6*0 9 4
  //   6*0 9 4 6*0 9 4 6*0 9 4 6*0 9 4 6*0 9 4 6*0 9 4 6*0 9 4 6*0 9 4 6*0 9 4 6*0 9 4 6*0 9 4 6*0 9 4 6*0
  //   9 4 6*0 9 4 6*0 9 4 6*0 9 4 6*0 9 4 6*0 9 4 6*0 9 4 6*0 9 4 6*0 9 4 646*0 9 4 6*0 9 4 6*0 9 4 6*0 9
  //   4 6*0 9 4 6*0 9 4 6*0 9 4 6*0 9 4 6*0 9 4 6*0 9 4 6*0 9 4 6*0 9 4 6*0 9 4 6*0 9 4 6*0 9 4 6*0 9 4
  //   646*0 9 4 6*0 9 4 6*0 9 4 6*0 9 4 6*0 9 4 6*0 9 4 6*0 9 4 6*0 9 4 6*0 9 4 6*0 9 4 6*0 9 4 6*0 9 4
  //   6*0 9 4 6*0 9 4 6*0 9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
  //   contents of rom_4 (hex, n*v repeats v):
  //   0 0 8 1 6*0 8 1 6*0 8 1 6*0 8 1 6*0 8 1 6*0 8 1 6*0 8 1 6*0 8 1 6*0 8 1 6*0 8 1 6*0 8 1 6*0 8 1 6*0
  //   8 1 6*0 8 1 6*0 8 1 6*0 8 1 6*0 20 1 6*0 20 1 6*0 20 1 6*0 20 1 6*0 20 1 6*0 20 1 6*0 20 1 6*0 20 1
  //   6*0 20 1 6*0 20 1 6*0 20 1 6*0 20 1 6*0 20 1 6*0 20 1 6*0 20 1 6*0 20 1 6*0 80 1 6*0 80 1 6*0 80 1
  //   6*0 80 1 6*0 80 1 6*0 80 1 6*0 80 1 6*0 80 1 6*0 80 1 6*0 80 1 6*0 80 1 6*0 80 1 6*0 80 1 6*0 80 1
  //   6*0 80 1 6*0 80 1 8*0 1 7*0 1 7*0 1 7*0 1 7*0 1 7*0 1 7*0 1 7*0 1 7*0 1 7*0 1 7*0 1 7*0 1 7*0 1 7*0
  //   1 7*0 1 7*0 1 9*0 1 7*0 1 7*0 1 7*0 1 7*0 1 7*0 1 7*0 1 7*0 1 7*0 1 7*0 1 7*0 1 7*0 1 7*0 1 7*0 1
  //   7*0 1 7*0 1 0 0 0 8 1 6*0 8 1 6*0 8 1 6*0 8 1 6*0 8 1 6*0 8 1 6*0 8 1 6*0 8 1 6*0 8 1 6*0 8 1 6*0 8
  //   1 6*0 8 1 6*0 8 1 6*0 8 1 6*0 8 1 6*0 8 1 6*0 20 1 6*0 20 1 6*0 20 1 6*0 20 1 6*0 20 1 6*0 20 1 6*0
  //   20 1 6*0 20 1 6*0 20 1 6*0 20 1 6*0 20 1 6*0 20 1 6*0 20 1 6*0 20 1 6*0 20 1 6*0 20 1 6*0 80 1 6*0
  //   80 1 6*0 80 1 6*0 80 1 6*0 80 1 6*0 80 1 6*0 80 1 6*0 80 1 6*0 80 1 6*0 80 1 6*0 80 1 6*0 80 1 6*0
  //   80 1 6*0 80 1 6*0 80 1 6*0 80 1 8*0 1 7*0 1 7*0 1 7*0 1 7*0 1 7*0 1 7*0 1 7*0 1 7*0 1 7*0 1 7*0 1
  //   7*0 1 7*0 1 7*0 1 7*0 1 7*0 1 9*0 1 7*0 1 7*0 1 7*0 1 7*0 1 7*0 1 7*0 1 7*0 1 7*0 1 7*0 1 7*0 1 7*0
  //   1 7*0 1 7*0 1 7*0 1 7*0 1 0 0 0 2 1 6*0 2 1 6*0 2 1 6*0 2 1 6*0 2 1 6*0 2 1 6*0 2 1 6*0 2 1 6*0 2 1
  //   6*0 2 1 6*0 2 1 6*0 2 1 6*0 2 1 6*0 2 1 6*0 2 1 6*0 2 1 6*0 8 4 6*0 8 4 6*0 8 4 6*0 8 4 6*0 8 4 6*0
  //   8 4 6*0 8 4 6*0 8 4 6*0 8 4 6*0 8 4 6*0 8 4 6*0 8 4 6*0 8 4 6*0 8 4 6*0 8 4 6*0 8 4 6*0 20 10 6*0 20
  //   10 6*0 20 10 6*0 20 10 6*0 20 10 6*0 20 10 6*0 20 10 6*0 20 10 6*0 20 10 6*0 20 10 6*0 20 10 6*0 20
  //   10 6*0 20 10 6*0 20 10 6*0 20 10 6*0 20 10 6*0 80 40 6*0 80 40 6*0 80 40 6*0 80 40 6*0 80 40 6*0 80
  //   40 6*0 80 40 6*0 80 40 6*0 80 40 6*0 80 40 6*0 80 40 6*0 80 40 6*0 80 40 6*0 80 40 6*0 80 40 6*0 80
  //   40 6*0 2 1 6*0 2 1 6*0 2 1 6*0 2 1 6*0 2 1 6*0 2 1 6*0 2 1 6*0 2 1 6*0 2 1 6*0 2 1 6*0 2 1 6*0 2 1
  //   6*0 2 1 6*0 2 1 6*0 2 1 6*0 2 1 6*0 8 4 6*0 8 4 6*0 8 4 6*0 8 4 6*0 8 4 6*0 8 4 6*0 8 4 6*0 8 4 6*0
  //   8 4 6*0 8 4 6*0 8 4 6*0 8 4 6*0 8 4 6*0 8 4 6*0 8 4 6*0 8 4 6*0 20 10 6*0 20 10 6*0 20 10 6*0 20 10
  //   6*0 20 10 6*0 20 10 6*0 20 10 6*0 20 10 6*0 20 10 6*0 20 10 6*0 20 10 6*0 20 10 6*0 20 10 6*0 20 10
  //   6*0 20 10 6*0 20 10 6*0 80 40 6*0 80 40 6*0 80 40 6*0 80 40 6*0 80 40 6*0 80 40 6*0 80 40 6*0 80 40
  //   6*0 80 40 6*0 80 40 6*0 80 40 6*0 80 40 6*0 80 40 6*0 80 40 6*0 80 40 6*0 80 40 6*0 2 1 6*0 2 1 6*0
  //   2 1 6*0 2 1 6*0 2 1 6*0 2 1 6*0 2 1 6*0 2 1 6*0 2 1 6*0 2 1 6*0 2 1 6*0 2 1 6*0 2 1 6*0 2 1 6*0 2 1
  //   6*0 2 1 6*0 8 4 6*0 8 4 6*0 8 4 6*0 8 4 6*0 8 4 6*0 8 4 6*0 8 4 6*0 8 4 6*0 8 4 6*0 8 4 6*0 8 4 6*0
  //   8 4 6*0 8 4 6*0 8 4 6*0 8 4 6*0 8 4 6*0 20 10 6*0 20 10 6*0 20 10 6*0 20 10 6*0 20 10 6*0 20 10 6*0
  //   20 10 6*0 20 10 6*0 20 10 6*0 20 10 6*0 20 10 6*0 20 10 6*0 20 10 6*0 20 10 6*0 20 10 6*0 20 10 6*0
  //   80 40 6*0 80 40 6*0 80 40 6*0 80 40 6*0 80 40 6*0 80 40 6*0 80 40 6*0 80 40 6*0 80 40 6*0 80 40 6*0
  //   80 40 6*0 80 40 6*0 80 40 6*0 80 40 6*0 80 40 6*0 80 40 6*0 6 7*0 6 7*0 6 7*0 6 7*0 6 7*0 6 7*0 6
  //   7*0 6 7*0 6 7*0 6 7*0 6 7*0 6 7*0 6 7*0 6 7*0 6 7*0 6 7*0 12 7*0 12 7*0 12 7*0 12 7*0 12 7*0 12 7*0
  //   12 7*0 12 7*0 12 7*0 12 7*0 12 7*0 12 7*0 12 7*0 12 7*0 12 7*0 12 7*0 42 7*0 42 7*0 42 7*0 42 7*0 42
  //   7*0 42 7*0 42 7*0 42 7*0 42 7*0 42 7*0 42 7*0 42 7*0 42 7*0 42 7*0 42 7*0 42 7*0 2 7*0 2 7*0 2 7*0 2
  //   7*0 2 7*0 2 7*0 2 7*0 2 7*0 2 7*0 2 7*0 2 7*0 2 7*0 2 7*0 2 7*0 2 7*0 2 7*0 9 7*0 9 7*0 9 7*0 9 7*0
  //   9 7*0 9 7*0 9 7*0 9 7*0 9 7*0 9 7*0 9 7*0 9 7*0 9 7*0 9 7*0 9 7*0 9 7*0 18 7*0 18 7*0 18 7*0 18 7*0
  //   18 7*0 18 7*0 18 7*0 18 7*0 18 7*0 18 7*0 18 7*0 18 7*0 18 7*0 18 7*0 18 7*0 18 7*0 48 7*0 48 7*0 48
  //   7*0 48 7*0 48 7*0 48 7*0 48 7*0 48 7*0 48 7*0 48 7*0 48 7*0 48 7*0 48 7*0 48 7*0 48 7*0 48 7*0 8 7*0
  //   8 7*0 8 7*0 8 7*0 8 7*0 8 7*0 8 7*0 8 7*0 8 7*0 8 7*0 8 7*0 8 7*0 8 7*0 8 7*0 8 7*0 8 7*0 21 7*0 21
  //   7*0 21 7*0 21 7*0 21 7*0 21 7*0 21 7*0 21 7*0 21 7*0 21 7*0 21 7*0 21 7*0 21 7*0 21 7*0 21 7*0 21
  //   7*0 24 7*0 24 7*0 24 7*0 24 7*0 24 7*0 24 7*0 24 7*0 24 7*0 24 7*0 24 7*0 24 7*0 24 7*0 24 7*0 24
  //   7*0 24 7*0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
  //   And so on.
  //   And another slice.
  //   This is one 8 bit "slice" of the output control signals.
endmodule

module ALU (
  input  [15:0] A,
  input  [15:0] B,
  input  carry_in,
  input  M,
  input  S0,
  input  S1,
  input  S2,
  input  S3,
  input  result_output_enable,
  input  clock,
  input  sim_only_reset,
  input  store_result,
  input  store_flags,
  output unclocked_zero,
  output clocked_zero,
  output unclocked_negative,
  output clocked_negative,
  output unclocked_carryborrow_out,
  output clocked_carryborrow_out,
  output unclocked_A___B,
  output clocked_A___B,
  output [15:0] tristate_clocked_result,
  output [15:0] unclocked_result,
  output [15:0] clocked_result
);

  wire n74ls181_1_a_b, n74ls181_1_carry_out_bar, n74ls181_2_a_b, n74ls181_2_carry_out_bar, n74ls181_3_a_b,
       n74ls181_3_carry_out_bar, n74ls181_4_a_b, n74ls181_4_carry_out_bar, not_2_out, or_1_out,
       safe_clock_enable_1_clock_out, safe_clock_enable_2_clock_out;

  not not_1 (unclocked_carryborrow_out, n74ls181_4_carry_out_bar);
  not not_2 (not_2_out, carry_in);
  and and_1 (unclocked_A___B, n74ls181_1_a_b, n74ls181_2_a_b, n74ls181_3_a_b, n74ls181_4_a_b);
  _74LS181 u_74ls181_1 (
    .B(B[3:0]), .A(A[3:0]), .M(M), .carry_in_bar(not_2_out), .carry_out_bar(n74ls181_1_carry_out_bar),
    .F(unclocked_result[3:0]), .A_B(n74ls181_1_a_b), .S0(S0), .S1(S1), .S2(S2), .S3(S3));  // open: Y, X
  _74LS181 u_74ls181_2 (
    .B(B[7:4]), .A(A[7:4]), .M(M), .carry_in_bar(n74ls181_1_carry_out_bar),
    .carry_out_bar(n74ls181_2_carry_out_bar), .F(unclocked_result[7:4]), .A_B(n74ls181_2_a_b), .S0(S0),
    .S1(S1), .S2(S2), .S3(S3));  // open: Y, X
  _74LS181 u_74ls181_3 (
    .B(B[11:8]), .A(A[11:8]), .M(M), .carry_in_bar(n74ls181_2_carry_out_bar),
    .carry_out_bar(n74ls181_3_carry_out_bar), .F(unclocked_result[11:8]), .A_B(n74ls181_3_a_b), .S0(S0),
    .S1(S1), .S2(S2), .S3(S3));  // open: Y, X
  _74LS181 u_74ls181_4 (
    .B(B[15:12]), .A(A[15:12]), .M(M), .carry_in_bar(n74ls181_3_carry_out_bar),
    .carry_out_bar(n74ls181_4_carry_out_bar), .F({unclocked_negative, unclocked_result[14:12]}),
    .A_B(n74ls181_4_a_b), .S0(S0), .S1(S1), .S2(S2), .S3(S3));  // open: Y, X
  or or_1 (or_1_out, unclocked_result[0], unclocked_result[1], unclocked_result[2], unclocked_result[3], unclocked_result[4], unclocked_result[5], unclocked_result[6], unclocked_result[7], unclocked_result[8], unclocked_result[9], unclocked_result[10], unclocked_result[11], unclocked_result[12], unclocked_result[13], unclocked_result[14], unclocked_negative);
  safe_clock_enable safe_clock_enable_1 (
    .clock_enable(store_result), .clock_in(clock), .clock_out(safe_clock_enable_1_clock_out));
  safe_clock_enable safe_clock_enable_2 (
    .clock_enable(store_flags), .clock_in(clock), .clock_out(safe_clock_enable_2_clock_out));
  not not_3 (unclocked_zero, or_1_out);
  Register #(.width(16)) result (
    .D({unclocked_negative, unclocked_result[14:0]}), .en(1'b1), .Q(clocked_result),
    .clk(safe_clock_enable_1_clock_out), .clr(sim_only_reset));
  assign tristate_clocked_result = result_output_enable ? clocked_result : 16'bz;  // Controlled_Buffer controlled_buffer_1
  Register #(.width(4)) register_1 (
    .D({unclocked_A___B, unclocked_carryborrow_out, unclocked_negative, unclocked_zero}), .en(1'b1),
    .Q({clocked_A___B, clocked_carryborrow_out, clocked_negative, clocked_zero}),
    .clk(safe_clock_enable_2_clock_out), .clr(sim_only_reset));

  assign unclocked_result[15] = unclocked_negative;
endmodule

module Clock (
  input  enable,
  input  Arduino_Crystal,
  input  Arduino_clock,
  output clock
);

  wire Crystal_clock_out, multiplexer_1_out;

  Clock_part Crystal_clock (.out(Crystal_clock_out));
  Multiplexer #(.enable("false")) multiplexer_1 (
    .in0(Arduino_clock), .in1(Crystal_clock_out), .out(multiplexer_1_out), .sel(Arduino_Crystal));
  safe_clock_enable safe_clock_enable_1 (.clock_enable(enable), .clock_in(multiplexer_1_out), .clock_out(clock));
endmodule

module _74LS181 (
  input  S0,
  input  S1,
  input  S2,
  input  S3,
  input  [3:0] B,
  input  [3:0] A,
  input  M,
  input  carry_in_bar,
  output Y,
  output carry_out_bar,
  output X,
  output [3:0] F,
  output A_B
);

  wire and_1_out, and_2_out, and_3_out, and_4_out, and_5_out, and_6_out, and_7_out, and_8_out, and_9_out,
       and_10_out, and_11_out, and_12_out, and_13_out, and_14_out, and_15_out, and_16_out, and_17_out,
       and_18_out, and_19_out, and_20_out, and_21_out, and_22_out, and_23_out, and_24_out, and_25_out,
       and_26_out, and_27_out, and_28_out, nand_1_out, nand_3_out, nor_1_out, nor_2_out, nor_3_out,
       nor_4_out, nor_5_out, nor_6_out, nor_7_out, nor_8_out, nor_10_out, nor_11_out, nor_12_out, not_1_out,
       not_2_out, not_3_out, not_4_out, not_5_out, xor_1_out, xor_2_out, xor_3_out, xor_4_out;

  not not_1 (not_1_out, B[3]);
  not not_2 (not_2_out, B[2]);
  not not_3 (not_3_out, B[1]);
  not not_4 (not_4_out, B[0]);
  not not_5 (not_5_out, M);
  and and_1 (and_1_out, B[3], S3, A[3]);
  and and_2 (and_2_out, A[3], S2, not_1_out);
  and and_3 (and_3_out, not_1_out, S1);
  and and_4 (and_4_out, S0, B[3]);
  and and_5 (and_5_out, B[2], S3, A[2]);
  and and_6 (and_6_out, A[2], S2, not_2_out);
  and and_7 (and_7_out, not_2_out, S1);
  and and_8 (and_8_out, S0, B[2]);
  and and_9 (and_9_out, B[1], S3, A[1]);
  and and_10 (and_10_out, A[1], S2, not_3_out);
  and and_11 (and_11_out, not_3_out, S1);
  and and_12 (and_12_out, S0, B[1]);
  and and_13 (and_13_out, B[0], S3, A[0]);
  and and_14 (and_14_out, A[0], S2, not_4_out);
  and and_15 (and_15_out, not_4_out, S1);
  and and_16 (and_16_out, S0, B[0]);
  nor nor_1 (nor_1_out, and_1_out, and_2_out);
  nor nor_2 (nor_2_out, and_3_out, and_4_out, A[3]);
  nor nor_3 (nor_3_out, and_5_out, and_6_out);
  nor nor_4 (nor_4_out, and_7_out, and_8_out, A[2]);
  nor nor_5 (nor_5_out, and_9_out, and_10_out);
  nor nor_6 (nor_6_out, and_11_out, and_12_out, A[1]);
  nor nor_7 (nor_7_out, and_13_out, and_14_out);
  nor nor_8 (nor_8_out, and_15_out, and_16_out, A[0]);
  xor xor_1 (xor_1_out, nor_1_out, nor_2_out);
  xor xor_2 (xor_2_out, nor_3_out, nor_4_out);
  xor xor_3 (xor_3_out, nor_5_out, nor_6_out);
  xor xor_4 (xor_4_out, nor_7_out, nor_8_out);
  and and_17 (and_17_out, nor_1_out, nor_4_out);
  and and_18 (and_18_out, nor_1_out, nor_3_out, nor_6_out);
  and and_19 (and_19_out, nor_1_out, nor_3_out, nor_5_out, nor_8_out);
  nand nand_1 (nand_1_out, nor_1_out, nor_3_out, nor_5_out, nor_7_out, carry_in_bar);
  nand nand_2 (X, nor_1_out, nor_3_out, nor_5_out, nor_7_out);
  and and_20 (and_20_out, carry_in_bar, nor_7_out, nor_5_out, nor_3_out, not_5_out);
  and and_21 (and_21_out, nor_5_out, nor_3_out, nor_8_out, not_5_out);
  and and_22 (and_22_out, nor_3_out, nor_6_out, not_5_out);
  and and_23 (and_23_out, nor_4_out, not_5_out);
  and and_24 (and_24_out, carry_in_bar, nor_7_out, nor_5_out, not_5_out);
  and and_25 (and_25_out, nor_5_out, nor_8_out, not_5_out);
  and and_26 (and_26_out, nor_6_out, not_5_out);
  and and_27 (and_27_out, carry_in_bar, nor_7_out, not_5_out);
  and and_28 (and_28_out, nor_8_out, not_5_out);
  nand nand_3 (nand_3_out, carry_in_bar, not_5_out);
  nor nor_9 (Y, nor_2_out, and_17_out, and_18_out, and_19_out);
  nor nor_10 (nor_10_out, and_20_out, and_21_out, and_22_out, and_23_out);
  nor nor_11 (nor_11_out, and_24_out, and_25_out, and_26_out);
  nor nor_12 (nor_12_out, and_27_out, and_28_out);
  or or_1 (carry_out_bar, ~Y, ~nand_1_out);  // OR_Gate
  xor xor_5 (F[3], xor_1_out, nor_10_out);
  xor xor_6 (F[2], xor_2_out, nor_11_out);
  xor xor_7 (F[1], xor_3_out, nor_12_out);
  xor xor_8 (F[0], xor_4_out, nand_3_out);
  and and_29 (A_B, F[3], F[2], F[1], F[0]);
endmodule

module safe_clock_enable (
  input  clock_enable,
  input  clock_in,
  output clock_out
);

  wire nor_1_out, nor_2_out, not_1_out, not_2_out;

  not not_1 (not_1_out, clock_enable);
  not not_2 (not_2_out, clock_in);
  nor nor_1 (nor_1_out, not_1_out, nor_2_out);
  nor nor_2 (nor_2_out, nor_1_out, not_2_out);
  and and_1 (clock_out, nor_1_out, clock_in);
endmodule

module register_bus_R (
  input  [15:0] \input ,
  input  input_enable,
  input  output_enable,
  input  clock,
  input  sim_only_reset,
  output [15:0] content,
  output [15:0] buffered_output
);

  wire safe_clock_enable_1_clock_out;

  safe_clock_enable safe_clock_enable_1 (
    .clock_enable(input_enable), .clock_in(clock), .clock_out(safe_clock_enable_1_clock_out));
  Register #(.width(16)) register_1 (
    .D(\input ), .en(1'b1), .Q(content), .clk(safe_clock_enable_1_clock_out), .clr(sim_only_reset));
  assign buffered_output = output_enable ? content : 16'bz;  // Controlled_Buffer controlled_buffer_1
endmodule

module register_bus_L (
  input  [15:0] \input ,
  input  input_enable,
  input  output_enable,
  input  clock,
  input  sim_only_reset,
  output [15:0] content,
  output [15:0] buffered_output
);

  wire safe_clock_enable_1_clock_out;

  safe_clock_enable safe_clock_enable_1 (
    .clock_enable(input_enable), .clock_in(clock), .clock_out(safe_clock_enable_1_clock_out));
  Register #(.width(16)) register_1 (
    .D(\input ), .en(1'b1), .Q(content), .clk(safe_clock_enable_1_clock_out), .clr(sim_only_reset));
  assign buffered_output = output_enable ? content : 16'bz;  // Controlled_Buffer controlled_buffer_1
endmodule

module program_counter (
  input  in,
  input  output_enable,
  input  [15:0] \input ,
  input  count,
  input  clock,
  input  reset,
  output [15:0] tristate_output,
  output [15:0] contents
);

  Counter #(.width(16), .max('hffff)) counter_1 (
    .load(in), .D(\input ), .count(count), .Q(contents), .clk(clock), .clr(reset));  // open: carry
  assign tristate_output = output_enable ? contents : 16'bz;  // Controlled_Buffer controlled_buffer_1
endmodule

module io_device (
  input  [7:0] in_1,
  input  [7:0] in_2,
  input  Prog_data_sel,
  input  Write_to_mem,
  input  Clock,
  output [7:0] out_6
);

  wire and_1_out, and_2_out, nand_1_out, not_1_out;

  nand nand_1 (nand_1_out, in_2[0], in_2[1], in_2[2], in_2[3], in_2[4], in_2[5], in_2[6], in_2[7]);
  not not_1 (not_1_out, nand_1_out);
  and and_1 (and_1_out, not_1_out, Prog_data_sel);
  and and_2 (and_2_out, and_1_out, Write_to_mem);
  Register register_1 (.D(in_1), .en(and_2_out), .Q(out_6), .clk(Clock), .clr(1'b0));
endmodule

module clipboard (
  input  in_1,
  input  in_2,
  output out_3,
  output out_4,
  output out_5,
  output clock_out
);

  wire A_IN, A_OUT, ACC_IN, ACC_OUT, ALU_A_IS_BUS, ALU_C_IN, ALU_CARRYBORROW_FLAG_CLOCKED,
       ALU_CARRYBORROW_FLAG_IMM, ALU_EQUAL_FLAG_CLOCKED, ALU_EQUAL_FLAG_IMM, ALU_M,
       ALU_NEGATIVE_FLAG_CLOCKED, ALU_NEGATIVE_FLAG_IMM, ALU_OUT, ALU_S0, ALU_S1, ALU_S2, ALU_S3,
       ALU_STORE_FLAGS, ALU_STORE_RESULT, ALU_ZERO_FLAG_CLOCKED, ALU_ZERO_FLAG_IMM, B_IN, B_OUT, C_IN, C_OUT,
       CLOCK_HALT, CONTROL_CLOCK, CU_CARRYBORROW_MIRROR, CU_EQUAL_MIRROR, CU_NEGATIVE_MIRROR, CU_STEP_RESET,
       CU_ZERO_MIRROR, IR_IN, MAR_IN, PC_COUNT, PC_IN, PC_OUT, SIM_ONLY_RESET, SP_IN, SP_OUT;
  wire [2:0] CU_MICROCODE_STEP;
  wire [7:0] A, ACC, ADDRESS, ALU_RESULT_CLOCKED, ALU_RESULT_IMM, B, BUS, C, CU_INSTRUCTION_MIRROR, IR, PC,
       SP;

  Button button_1 (.out(SIM_ONLY_RESET));
  LED led_1 (.in(ACC_IN));
  LED led_2 (.in(ACC_OUT));
  LED led_3 (.in(A_IN));
  LED led_4 (.in(A_OUT));
  LED led_5 (.in(B_IN));
  LED led_6 (.in(B_OUT));
  LED led_7 (.in(C_IN));
  LED led_8 (.in(C_OUT));
  LED led_9 (.in(ALU_STORE_RESULT));
  LED led_10 (.in(ALU_STORE_FLAGS));
  LED led_11 (.in(ALU_OUT));
  LED led_12 (.in(ALU_A_IS_BUS));
  LED led_13 (.in(ALU_S0));
  LED led_14 (.in(ALU_S1));
  LED led_15 (.in(ALU_S2));
  LED led_16 (.in(ALU_S3));
  LED led_17 (.in(ALU_M));
  LED led_18 (.in(ALU_C_IN));
  LED led_19 (.in(MAR_IN));
  LED led_20 (.in(out_4));
  LED led_21 (.in(out_5));
  LED led_22 (.in(out_3));
  LED led_23 (.in(SP_IN));
  LED led_24 (.in(SP_OUT));
  LED led_25 (.in(PC_IN));
  LED led_26 (.in(PC_OUT));
  LED led_27 (.in(PC_COUNT));
  LED led_28 (.in(IR_IN));
  LED led_29 (.in(CU_STEP_RESET));
  LED led_30 (.in(CLOCK_HALT));
  LED led_31 (.in(BUS[7]));
  LED led_32 (.in(BUS[6]));
  LED led_33 (.in(PC[6]));
  LED led_34 (.in(PC[7]));
  LED led_35 (.in(IR[6]));
  LED led_36 (.in(IR[7]));
  LED led_37 (.in(SP[7]));
  LED led_38 (.in(SP[6]));
  LED led_39 (.in(ACC[7]));
  LED led_40 (.in(ACC[6]));
  LED led_41 (.in(A[6]));
  LED led_42 (.in(A[7]));
  LED led_43 (.in(B[7]));
  LED led_44 (.in(B[6]));
  LED led_45 (.in(C[6]));
  LED led_46 (.in(C[7]));
  LED led_47 (.in(ADDRESS[7]));
  LED led_48 (.in(ADDRESS[6]));
  LED led_49 (.in(BUS[4]));
  LED led_50 (.in(BUS[3]));
  LED led_51 (.in(BUS[2]));
  LED led_52 (.in(BUS[5]));
  LED led_53 (.in(PC[2]));
  LED led_54 (.in(PC[5]));
  LED led_55 (.in(PC[3]));
  LED led_56 (.in(PC[4]));
  LED led_57 (.in(IR[4]));
  LED led_58 (.in(IR[2]));
  LED led_59 (.in(IR[5]));
  LED led_60 (.in(IR[3]));
  LED led_61 (.in(SP[5]));
  LED led_62 (.in(SP[2]));
  LED led_63 (.in(SP[3]));
  LED led_64 (.in(SP[4]));
  LED led_65 (.in(ACC[4]));
  LED led_66 (.in(ACC[5]));
  LED led_67 (.in(ACC[2]));
  LED led_68 (.in(ACC[3]));
  LED led_69 (.in(A[3]));
  LED led_70 (.in(A[5]));
  LED led_71 (.in(A[4]));
  LED led_72 (.in(A[2]));
  LED led_73 (.in(B[2]));
  LED led_74 (.in(B[4]));
  LED led_75 (.in(B[5]));
  LED led_76 (.in(B[3]));
  LED led_77 (.in(C[5]));
  LED led_78 (.in(C[3]));
  LED led_79 (.in(C[4]));
  LED led_80 (.in(C[2]));
  LED led_81 (.in(ADDRESS[4]));
  LED led_82 (.in(ADDRESS[3]));
  LED led_83 (.in(ADDRESS[2]));
  LED led_84 (.in(ADDRESS[5]));
  // Probe on BUS
  LED led_85 (.in(BUS[1]));
  LED led_86 (.in(BUS[0]));
  // Probe on PC
  LED led_87 (.in(PC[1]));
  LED led_88 (.in(PC[0]));
  // Probe on IR
  LED led_89 (.in(IR[1]));
  LED led_90 (.in(IR[0]));
  // Probe on SP
  LED led_91 (.in(SP[0]));
  LED led_92 (.in(SP[1]));
  // Probe on ACC
  LED led_93 (.in(ACC[0]));
  LED led_94 (.in(ACC[1]));
  // Probe on A
  LED led_95 (.in(A[1]));
  LED led_96 (.in(A[0]));
  // Probe on B
  LED led_97 (.in(B[1]));
  LED led_98 (.in(B[0]));
  // Probe on C
  LED led_99 (.in(C[1]));
  LED led_100 (.in(C[0]));
  // Probe on ADDRESS
  LED led_101 (.in(ADDRESS[0]));
  LED led_102 (.in(ADDRESS[1]));
  // Probe on BUS
  // Probe on BUS
  // Probe on PC
  // Probe on PC
  // Probe on IR
  // Probe on IR
  // Probe on SP
  // Probe on SP
  // Probe on ACC
  // Probe on ACC
  // Probe on A
  // Probe on A
  // Probe on B
  // Probe on B
  // Probe on C
  // Probe on C
  // Probe on ADDRESS
  // Probe on ADDRESS
  LED led_103 (.in(ALU_RESULT_IMM[7]));
  LED led_104 (.in(ALU_RESULT_IMM[6]));
  LED led_105 (.in(ALU_RESULT_CLOCKED[7]));
  LED led_106 (.in(ALU_RESULT_CLOCKED[6]));
  LED led_107 (.in(ALU_ZERO_FLAG_IMM));
  LED led_108 (.in(ALU_NEGATIVE_FLAG_IMM));
  LED led_109 (.in(ALU_CARRYBORROW_FLAG_IMM));
  LED led_110 (.in(ALU_EQUAL_FLAG_IMM));
  LED led_111 (.in(ALU_ZERO_FLAG_CLOCKED));
  LED led_112 (.in(ALU_NEGATIVE_FLAG_CLOCKED));
  LED led_113 (.in(ALU_CARRYBORROW_FLAG_CLOCKED));
  LED led_114 (.in(ALU_EQUAL_FLAG_CLOCKED));
  LED led_115 (.in(CU_INSTRUCTION_MIRROR[7]));
  LED led_116 (.in(CU_MICROCODE_STEP[2]));
  LED led_117 (.in(CU_ZERO_MIRROR));
  LED led_118 (.in(CU_NEGATIVE_MIRROR));
  LED led_119 (.in(CU_CARRYBORROW_MIRROR));
  LED led_120 (.in(CU_EQUAL_MIRROR));
  LED led_121 (.in(clock_out));
  LED led_122 (.in(CONTROL_CLOCK));
  LED led_123 (.in(ALU_RESULT_IMM[5]));
  LED led_124 (.in(ALU_RESULT_IMM[4]));
  LED led_125 (.in(ALU_RESULT_IMM[2]));
  LED led_126 (.in(ALU_RESULT_IMM[3]));
  LED led_127 (.in(ALU_RESULT_CLOCKED[3]));
  LED led_128 (.in(ALU_RESULT_CLOCKED[5]));
  LED led_129 (.in(ALU_RESULT_CLOCKED[2]));
  LED led_130 (.in(ALU_RESULT_CLOCKED[4]));
  LED led_131 (.in(CU_INSTRUCTION_MIRROR[6]));
  LED led_132 (.in(CU_INSTRUCTION_MIRROR[4]));
  LED led_133 (.in(CU_INSTRUCTION_MIRROR[3]));
  LED led_134 (.in(CU_INSTRUCTION_MIRROR[5]));
  LED led_135 (.in(CU_MICROCODE_STEP[0]));
  LED led_136 (.in(CU_MICROCODE_STEP[1]));
  // Probe on ALU_RESULT_IMM
  LED led_137 (.in(ALU_RESULT_IMM[0]));
  LED led_138 (.in(ALU_RESULT_IMM[1]));
  // Probe on ALU_RESULT_CLOCKED
  LED led_139 (.in(ALU_RESULT_CLOCKED[1]));
  LED led_140 (.in(ALU_RESULT_CLOCKED[0]));
  LED led_141 (.in(CU_INSTRUCTION_MIRROR[2]));
  LED led_142 (.in(CU_INSTRUCTION_MIRROR[0]));
  LED led_143 (.in(CU_INSTRUCTION_MIRROR[1]));
  // Probe on ALU_RESULT_IMM
  // Probe on ALU_RESULT_IMM
  // Probe on ALU_RESULT_CLOCKED
  // Probe on ALU_RESULT_CLOCKED
  // Probe on CU_INSTRUCTION_MIRROR
  // Probe on CU_INSTRUCTION_MIRROR
  // Probe on CU_INSTRUCTION_MIRROR
  // Probe on CU_MICROCODE_STEP
  // Probe on CU_MICROCODE_STEP
  // Probe on CU_MICROCODE_STEP

  // Other names for the same wires on the sheet: DATA_CLOCK = clock_out; EXT_CLOCK_PULSE = in_2;
  //   PROG_DATA_MEM = out_3; READ_FROM_MEM = out_5; RESET = in_1; WRITE_TO_MEM = out_4

  // Notes on the sheet:
  //   BIN
  //   BIN
  //   HEX
  //   BIN
  //   HEX
  //   DEC
  //   BIN
  //   HEX
  //   DEC
  //   BIN
  //   HEX
  //   DEC
  //   HEX
  //   DEC
  //   BIN
  //   HEX
  //   DEC
  //   BIN
  //   HEX
  //   DEC
  //   BIN
  //   HEX
  //   DEC
  //   DEC
  //   BIN
  //   HEX
  //   DEC
  //   BIN
  //   HEX
  //   DEC
  //   BIN
  //   HEX
  //   DEC
  //   BIN
  //   HEX
  //   DEC
  //   BIN
  //   HEX
  //   DEC
endmodule

module schem_export (
  input  Halt,
  input  Reset,
  input  Auto_Manual,
  input  Manual_clock,
  output Clock,
  output Control_Clock
);

  wire Auto_clock_out, nand_1_out, nand_2_out, nand_3_out, nand_4_out, nand_5_out, nand_6_out, nand_7_out,
       nand_8_out, nor_1_out, nor_2_out, nor_3_out, nor_4_out, not_1_out, not_2_out;

  Clock_part Auto_clock (.out(Auto_clock_out));
  nand nand_1 (nand_1_out, Auto_Manual, Auto_Manual);
  nor nor_1 (nor_1_out, Halt, Reset);
  nand nand_2 (nand_2_out, Auto_Manual, Manual_clock);
  nand nand_3 (nand_3_out, nand_1_out, Auto_clock_out);
  nand nand_4 (nand_4_out, nor_1_out, nor_1_out);
  nand nand_5 (nand_5_out, nand_2_out, nand_3_out);
  nor nor_2 (nor_2_out, nand_5_out, nand_5_out);
  nor nor_3 (nor_3_out, nand_4_out, nor_4_out);
  nor nor_4 (nor_4_out, nor_3_out, nor_2_out);
  nand nand_6 (nand_6_out, nor_3_out, nand_5_out);
  nand nand_7 (nand_7_out, nand_6_out, nand_6_out);
  nand nand_8 (nand_8_out, nand_7_out, nand_7_out);
  J_K_Flip_Flop j_k_ff_1 (
    .J(1'b1), .clk(nand_7_out), .K(1'b1), .Q(Clock), .preset(1'b0), .en(1'b1), .reset(not_1_out));  // open: Qn
  not not_1 (not_1_out, nor_1_out);
  J_K_Flip_Flop j_k_ff_2 (
    .J(1'b1), .clk(nand_8_out), .K(1'b1), .Q(Control_Clock), .preset(1'b0), .en(1'b1), .reset(not_2_out));  // open: Qn
  not not_2 (not_2_out, nor_1_out);

  // Notes on the sheet:
  //   Safe clock enable
endmodule

module ALU_comparison_test (
  input  [7:0] in_1,
  input  [7:0] in_2,
  input  in_3,
  input  in_4,
  input  in_5,
  input  in_6,
  input  in_7,
  input  in_8,
  output out_9,
  output out_10,
  output [7:0] out_11
);

  wire n74ls181_1_a_b, n74ls181_1_carry_out_bar, n74ls181_2_a_b, n74ls181_2_carry_out_bar, not_2_out;

  not not_1 (out_10, n74ls181_2_carry_out_bar);
  not not_2 (not_2_out, in_3);
  and and_1 (out_9, n74ls181_1_a_b, n74ls181_2_a_b);
  _74LS181 u_74ls181_1 (
    .B(in_2[3:0]), .A(in_1[3:0]), .M(in_4), .carry_in_bar(not_2_out),
    .carry_out_bar(n74ls181_1_carry_out_bar), .F(out_11[3:0]), .A_B(n74ls181_1_a_b), .S0(in_5), .S1(in_6),
    .S2(in_7), .S3(in_8));  // open: Y, X
  _74LS181 u_74ls181_2 (
    .B(in_2[7:4]), .A(in_1[7:4]), .M(in_4), .carry_in_bar(n74ls181_1_carry_out_bar),
    .carry_out_bar(n74ls181_2_carry_out_bar), .F(out_11[7:4]), .A_B(n74ls181_2_a_b), .S0(in_5), .S1(in_6),
    .S2(in_7), .S3(in_8));  // open: Y, X
  // Probe on in_2[3:0]
  // Probe on in_1[3:0]
endmodule

module new_clock_test (
  input  clock_enable,
  input  R,
  input  clock_in,
  input  S,
  input  in_5,
  input  clock_enable_2,
  input  in_7,
  input  clock_in_2,
  input  in_9,
  input  in_10,
  input  in_11,
  input  in_12,
  input  in_13,
  input  in_14,
  output clock_out,
  output out_16,
  output out_17
);

  wire and_1_out, and_2_out, nor_1_out, nor_2_out, nor_3_out, nor_4_out, nor_5_out, nor_6_out, not_1_out,
       not_2_out;

  nor nor_1 (nor_1_out, R, nor_2_out);
  nor nor_2 (nor_2_out, nor_1_out, S);
  safe_clock_enable safe_clock_enable_1 (.clock_enable(in_5), .clock_in(in_7), .clock_out(out_16));
  safe_clock_enable_disable safe_clock_enable_disable_1 (.clock_enable(in_13), .clock_in(in_14), .clock_out(out_17));
  not not_1 (not_1_out, clock_enable);
  not not_2 (not_2_out, clock_in);
  nor nor_3 (nor_3_out, not_1_out, nor_4_out);
  nor nor_4 (nor_4_out, nor_3_out, not_2_out);
  and and_1 (and_1_out, nor_3_out, clock_in);
  J_K_Flip_Flop j_k_ff_1 (
    .J(clock_enable_2), .clk(clock_in_2), .K(in_9), .preset(in_10), .en(in_11), .reset(in_12));  // open: Q, Qn
  and and_2 (and_2_out, not_1_out, not_2_out);
  nor nor_5 (nor_5_out, and_2_out, nor_6_out);
  nor nor_6 (nor_6_out, nor_5_out, and_1_out);
  and and_3 (clock_out, nor_5_out, clock_in);

  // Notes on the sheet:
  //   Q
  //   Q'
  //   Reset
  //   Set
endmodule

module safe_clock_enable_disable (
  input  clock_enable,
  input  clock_in,
  output clock_out
);

  wire and_1_out, and_2_out, nor_1_out, nor_2_out, nor_3_out, nor_4_out, not_1_out, not_2_out;

  not not_1 (not_1_out, clock_enable);
  nor nor_1 (nor_1_out, not_1_out, nor_2_out);
  nor nor_2 (nor_2_out, nor_1_out, not_2_out);
  not not_2 (not_2_out, clock_in);
  and and_1 (and_1_out, nor_1_out, clock_in);
  and and_2 (and_2_out, not_1_out, not_2_out);
  nor nor_3 (nor_3_out, and_2_out, nor_4_out);
  nor nor_4 (nor_4_out, nor_3_out, and_1_out);
  and and_3 (clock_out, nor_3_out, clock_in);

  // Notes on the sheet:
  //   Reset
  //   Set
endmodule
